// Logisim project s-mips.circ as structural Verilog: 32 circuits, main circuit S-MIPS Board
module S_MIPS_Board (
  output halt
);

  wire button_1_out, CLK, CS, d_ff_1_q, R_W, Reset_out, RST, TTY_EN;
  wire [2:0] KDB;
  wire [3:0] Mask, ram_1_read_time, ram_1_write_time;
  wire [6:0] KDB_DATA, TTY_DATA;
  wire [15:0] Addr;
  wire [31:0] ram_1_data_out_0, ram_1_data_out_1, ram_1_data_out_2, ram_1_data_out_3, s_mips_1_ram_in_0,
       s_mips_1_ram_in_1, s_mips_1_ram_in_2, s_mips_1_ram_in_3;

  TTY #(.rows(25), .cols(80)) tty_1 (.data(TTY_DATA), .clk(CLK), .we(TTY_EN), .clr(RST));
  RAM ram_1 (
    .Address(Addr), .Data_Out_0(ram_1_data_out_0), .Data_Out_1(ram_1_data_out_1),
    .Data_Out_2(ram_1_data_out_2), .Data_Out_3(ram_1_data_out_3), .Data_In_0(s_mips_1_ram_in_0),
    .Data_In_1(s_mips_1_ram_in_1), .Data_In_2(s_mips_1_ram_in_2), .Data_In_3(s_mips_1_ram_in_3), .Mask(Mask),
    .nRead_Write(R_W), .Chip_Select(CS), .Read_Time(ram_1_read_time), .Reset(button_1_out),
    .Write_Time(ram_1_write_time));
  Button button_1 (.out(button_1_out));
  Keyboard #(.buflen(64)) keyboard_1 (.clk(CLK), .re(KDB[0]), .clr(KDB[1]), .avail(KDB[2]), .data(KDB_DATA));
  S_MIPS s_mips_1 (
    .Kbd_Enable(KDB[0]), .Address(Addr), .Kbd_Clear(KDB[1]), .Kbd_Available(KDB[2]),
    .RAM_In_0(s_mips_1_ram_in_0), .Kbd_ASCII_Data(KDB_DATA), .RAM_In_1(s_mips_1_ram_in_1),
    .RAM_In_2(s_mips_1_ram_in_2), .RAM_In_3(s_mips_1_ram_in_3), .Reset(RST), .RAM_Out_0(ram_1_data_out_0),
    .RAM_Out_1(ram_1_data_out_1), .Stop(halt), .RAM_Out_2(ram_1_data_out_2), .RAM_Out_3(ram_1_data_out_3),
    .Mask(Mask), .Read_Time(ram_1_read_time), .Write_Time(ram_1_write_time), .nRead_Write(R_W),
    .Chip_Select(CS), .TTY_Enable(TTY_EN), .TTY_ASCII_Data(TTY_DATA), .Clock(CLK));
  D_Flip_Flop d_ff_1 (.clk(CLK), .D(1'b1), .Q(d_ff_1_q), .reset(Reset_out));  // open: Qn, preset, en
  Button Reset (.out(Reset_out));
  Clock clock_1 (.out(CLK));
  D_Flip_Flop d_ff_2 (.clk(CLK), .D(d_ff_1_q), .Qn(RST), .reset(Reset_out));  // open: Q, preset, en

  // Notes on the sheet:
  //   Keyboard
endmodule

module RAM (
  input  [15:0] Address,
  input  [31:0] Data_In_0,
  input  [31:0] Data_In_1,
  input  [31:0] Data_In_2,
  input  [31:0] Data_In_3,
  input  [3:0] Mask,
  input  nRead_Write,
  input  Chip_Select,
  input  Reset,
  output [31:0] Data_Out_0,
  output [31:0] Data_Out_1,
  output [31:0] Data_Out_2,
  output [31:0] Data_Out_3,
  output [3:0] Read_Time,
  output [3:0] Write_Time
);

  wire and_2_out, and_3_out, and_4_out, and_5_out, and_6_out, and_7_out, and_8_out, and_9_out, Changed, CLK,
       comparator_2_eq, comparator_3_eq, comparator_4_eq, comparator_5_eq, comparator_6_eq, Count,
       demultiplexer_3_out0, Idle, Idle_q, Load, Load0, Load1, nand_1_out, or_1_out, or_2_out, or_3_out,
       or_4_out, or_5_out, or_6_out, or_7_out, or_8_out, or_9_out, or_10_out, Proc_q, Update_Mem, Zero_Time;
  wire [3:0] counter_1_q, multiplexer_1_out, subtractor_1_out;
  wire [31:0] register_1_q, register_2_q, register_3_q, register_4_q, register_5_q;

  // Probe on 4'b0011
  // Probe on 4'b0101
  Multiplexer #(.width(4), .enable("false")) multiplexer_1 (
    .in0(4'b0011), .in1(4'b0101), .out(multiplexer_1_out), .sel(nRead_Write));
  or or_1 (or_1_out, Idle, Update_Mem);
  or or_2 (or_2_out, ~Chip_Select, Reset);  // OR_Gate
  Subtractor #(.width(4)) subtractor_1 (.a(multiplexer_1_out), .b(4'b0010), .out(subtractor_1_out));  // open: bin, bout
  Demultiplexer #(.enable("false")) demultiplexer_1 (.out0(Idle), .out1(Load0), .in(Idle_q), .sel(Changed));
  D_Flip_Flop u_Idle (.clk(CLK), .D(or_1_out), .Q(Idle_q), .preset(or_2_out));  // open: Qn, en, reset
  // Probe on counter_1_q
  Counter #(.width(4), .max('hf)) counter_1 (
    .load(Load), .D(subtractor_1_out), .count(Count), .Q(counter_1_q), .clk(CLK), .clr(or_3_out));  // open: carry
  or or_3 (or_3_out, ~Chip_Select, Reset);  // OR_Gate
  Comparator_part #(.width(4), .mode("unsigned")) comparator_1 (
    .a(4'b0000), .b(counter_1_q), .eq(Zero_Time));  // open: gt, lt
  or or_4 (or_4_out, Count, Load0, Load1);
  Register #(.width(32)) register_1 (.D(Data_In_0), .en(Chip_Select), .Q(register_1_q), .clk(CLK), .clr(or_5_out));
  or or_5 (or_5_out, ~Chip_Select, Reset);  // OR_Gate
  Register #(.width(32)) register_2 (.D(Data_In_1), .en(Chip_Select), .Q(register_2_q), .clk(CLK), .clr(or_6_out));
  or or_6 (or_6_out, ~Chip_Select, Reset);  // OR_Gate
  Register #(.width(32)) register_3 (.D(Data_In_2), .en(Chip_Select), .Q(register_3_q), .clk(CLK), .clr(or_7_out));
  or or_7 (or_7_out, ~Chip_Select, Reset);  // OR_Gate
  Register #(.width(32)) register_4 (.D(Data_In_3), .en(Chip_Select), .Q(register_4_q), .clk(CLK), .clr(or_8_out));
  or or_8 (or_8_out, ~Chip_Select, Reset);  // OR_Gate
  Register #(.width(32)) register_5 (
    .D({{11{1'b1}}, nRead_Write, Mask, Address}), .en(Chip_Select), .Q(register_5_q), .clk(CLK),
    .clr(or_9_out));
  or or_9 (or_9_out, ~Chip_Select, Reset);  // OR_Gate
  D_Flip_Flop Proc (.clk(CLK), .D(or_4_out), .Q(Proc_q), .reset(or_10_out));  // open: Qn, preset, en
  or or_10 (or_10_out, ~Chip_Select, Reset);  // OR_Gate
  Demultiplexer #(.enable("false")) demultiplexer_2 (
    .out0(Count), .out1(Update_Mem), .in(demultiplexer_3_out0), .sel(Zero_Time));
  Demultiplexer #(.enable("false")) demultiplexer_3 (
    .out0(demultiplexer_3_out0), .out1(Load1), .in(Proc_q), .sel(Changed));
  Clock clock_1 (.out(CLK));
  Comparator_part #(.width(32)) comparator_2 (.a(register_1_q), .b(Data_In_0), .eq(comparator_2_eq));  // open: gt, lt
  Comparator_part #(.width(32)) comparator_3 (.a(register_2_q), .b(Data_In_1), .eq(comparator_3_eq));  // open: gt, lt
  Comparator_part #(.width(32)) comparator_4 (.a(register_3_q), .b(Data_In_2), .eq(comparator_4_eq));  // open: gt, lt
  Comparator_part #(.width(32)) comparator_5 (.a(register_4_q), .b(Data_In_3), .eq(comparator_5_eq));  // open: gt, lt
  Comparator_part #(.width(32)) comparator_6 (
    .a(register_5_q), .b({{11{1'b1}}, nRead_Write, Mask, Address}), .eq(comparator_6_eq));  // open: gt, lt
  nand nand_1 (nand_1_out, comparator_6_eq, comparator_2_eq, comparator_3_eq, comparator_4_eq, comparator_5_eq);
  and and_1 (Changed, nand_1_out, Chip_Select);
  or or_11 (Load, Count, Load1, Load0);
  and and_2 (and_2_out, Mask[0], Update_Mem, nRead_Write);
  and and_3 (and_3_out, Mask[1], Update_Mem, nRead_Write);
  and and_4 (and_4_out, Mask[2], Update_Mem, nRead_Write);
  and and_5 (and_5_out, Mask[3], Update_Mem, nRead_Write);
  RAM_part #(.addrWidth(16), .dataWidth(32), .bus("separate")) ram_1 (
    .addr(Address), .din(Data_In_0), .data(Data_Out_0), .str(and_2_out), .sel(Chip_Select), .clk(CLK),
    .ld(and_6_out), .clr(Reset));
  and and_6 (and_6_out, ~nRead_Write, Idle);  // AND_Gate
  RAM_part #(.addrWidth(16), .dataWidth(32), .bus("separate")) ram_2 (
    .addr(Address), .din(Data_In_1), .data(Data_Out_1), .str(and_3_out), .sel(Chip_Select), .clk(CLK),
    .ld(and_7_out), .clr(Reset));
  and and_7 (and_7_out, ~nRead_Write, Idle);  // AND_Gate
  RAM_part #(.addrWidth(16), .dataWidth(32), .bus("separate")) ram_3 (
    .addr(Address), .din(Data_In_2), .data(Data_Out_2), .str(and_4_out), .sel(Chip_Select), .clk(CLK),
    .ld(and_8_out), .clr(Reset));
  and and_8 (and_8_out, ~nRead_Write, Idle);  // AND_Gate
  RAM_part #(.addrWidth(16), .dataWidth(32), .bus("separate")) ram_4 (
    .addr(Address), .din(Data_In_3), .data(Data_Out_3), .str(and_5_out), .sel(Chip_Select), .clk(CLK),
    .ld(and_9_out), .clr(Reset));
  and and_9 (and_9_out, ~nRead_Write, Idle);  // AND_Gate

  assign Read_Time = 4'b0011;
  assign Write_Time = 4'b0101;

  // Other names for the same wires on the sheet: M0 = Mask[0]; M1 = Mask[1]; M2 = Mask[2]; M3 = Mask[3];
  //   RW = nRead_Write; CLR = Reset; CS = Chip_Select; Load2 = Count

  // Notes on the sheet:
  //   BANK0
  //   BANK1
  //   BANK2
  //   BANK3
endmodule

module S_MIPS (
  input  Kbd_Available,
  input  [3:0] Read_Time,
  input  [6:0] Kbd_ASCII_Data,
  input  [3:0] Write_Time,
  input  [31:0] RAM_Out_0,
  input  [31:0] RAM_Out_1,
  input  [31:0] RAM_Out_2,
  input  Reset,
  input  Clock,
  input  [31:0] RAM_Out_3,
  output Kbd_Enable,
  output [3:0] Mask,
  output [15:0] Address,
  output [31:0] RAM_In_0,
  output Kbd_Clear,
  output [31:0] RAM_In_1,
  output TTY_Enable,
  output nRead_Write,
  output [31:0] RAM_In_2,
  output [6:0] TTY_ASCII_Data,
  output Chip_Select,
  output [31:0] RAM_In_3,
  output Stop
);

  wire ALU_I, DC, EN_DC, EN_IC, EN_IF, EN_PC, EN_RF, HALT_I, JMP_I, KBD_I, L_I, R_W_I, READY, S_I, START,
       TR_I, TTY_I;
  wire [17:0] ADDRESS_t;
  wire [31:0] DATA, M_ADDRESS;

  ControlUnit controlunit_1 (
    .Clock(Clock), .Reset(Reset), .halt(HALT_I), .JMPI(JMP_I), .TRI(TR_I), .ALUI(ALU_I), .LI(L_I), .SI(S_I),
    .EnIF(EN_IF), .EnRF(EN_RF), .EnPC(EN_PC), .End(Stop), .ttyI(TTY_I), .EnTTY(TTY_Enable), .Start(START),
    .Ready(READY), .EnIC(EN_IC), .EnDC(EN_DC), .EnKBD(Kbd_Enable), .kbdI(KBD_I), .R_WI(R_W_I), .DC(DC));
  CacheMemory cachememory_1 (
    .Address(ADDRESS_t), .RAMOut0(RAM_Out_0), .RAMOut1(RAM_Out_1), .Clock(Clock), .Reset(Reset),
    .EnIC(EN_IC), .EnDC(EN_DC), .RAMOut2(RAM_Out_2), .RAMOut3(RAM_Out_3), .R_WDC(R_W_I), .RT(Read_Time),
    .WT(Write_Time), .RAMAddress(Address), .R_W(nRead_Write), .CS(Chip_Select), .Ready(READY),
    .RAMIn0(RAM_In_0), .RAMIn1(RAM_In_1), .RAMIn2(RAM_In_2), .RAMIn3(RAM_In_3), .Data(DATA),
    .M_Address(M_ADDRESS), .DC(DC));
  D_Flip_Flop d_ff_1 (.clk(Clock), .D(Reset), .Q(START));  // open: Qn, preset, en, reset
  DataPath datapath_1 (
    .Clock(Clock), .Reset(Reset), .EnIF(EN_IF), .EnPC(EN_PC), .kbdAavil(Kbd_Available),
    .kbdData(Kbd_ASCII_Data), .EnRF(EN_RF), .M_Address(M_ADDRESS), .Address(ADDRESS_t), .haltI(HALT_I),
    .JMPI(JMP_I), .R_WI(R_W_I), .TRI(TR_I), .ALUI(ALU_I), .LI(L_I), .SI(S_I), .ttyI(TTY_I), .kbdI(KBD_I),
    .Data(DATA), .ttyData(TTY_ASCII_Data));

  assign Kbd_Clear = Reset;
  assign Mask = 4'b1111;

  // Other names for the same wires on the sheet: CLK = Clock; CS = Chip_Select; KBD_AVAIL = Kbd_Available;
  //   CLR = Reset; KBD_CLR = Reset; KBD_DATA[6:0] = Kbd_ASCII_Data; RAM_A[15:0] = Address;
  //   RAM_INPUT_0[31:0] = RAM_In_0; RAM_INPUT_1[31:0] = RAM_In_1; RAM_INPUT_2[31:0] = RAM_In_2;
  //   RAM_INPUT_3[31:0] = RAM_In_3; RAM_OUTPUT_0[31:0] = RAM_Out_0; RAM_OUTPUT_1[31:0] = RAM_Out_1;
  //   RAM_OUTPUT_2[31:0] = RAM_Out_2; RAM_OUTPUT_3[31:0] = RAM_Out_3; RW = nRead_Write;
  //   TTY_DATA[6:0] = TTY_ASCII_Data

  // Notes on the sheet:
  //   RAM ADDRESS
  //   DATA FROM RAM
  //   Control Unit 
  //   KEYBOARD
  //   TTY
  //   SEQUENCING
  //   DATA TO RAM
  //   Cache Memory
  //   RAM TIMING
  //   RAM CONTROL
  //   DATA WRITE MASK
  //   Data Path
endmodule

// CU
module ControlUnit (
  input  Clock,
  input  Reset,
  input  Start,
  input  halt,
  input  JMPI,
  input  TRI,
  input  ALUI,
  input  LI,
  input  SI,
  input  R_WI,
  input  ttyI,
  input  kbdI,
  input  Ready,
  output EnIC,
  output EnIF,
  output EnDC,
  output DC,
  output EnRF,
  output EnTTY,
  output EnKBD,
  output EnPC,
  output End
);

  wire ALU_q, BRANCH, CONTINUE, DC_q, demultiplexer_1_out0, demultiplexer_2_out0, demultiplexer_2_out3,
       demultiplexer_2_out4, demultiplexer_2_out5, demultiplexer_3_out0, demultiplexer_4_out0,
       demultiplexer_5_out1, demultiplexer_6_out0, demultiplexer_6_out1, EN_RF0, EN_RF1, IC_q, IF_q, KBD,
       or_4_out, or_7_out, or_9_out, PC_q, REG_FILE, RF_q, START_q;
  wire [2:0] SELECTOR;

  D_Flip_Flop u_START (.clk(Clock), .D(Start), .Q(START_q), .reset(Reset));  // open: Qn, preset, en
  or or_1 (SELECTOR[2], LI, SI);
  or or_2 (SELECTOR[1], TRI, ALUI);
  or or_3 (SELECTOR[0], JMPI, ALUI, SI);
  D_Flip_Flop PC (.clk(Clock), .D(EnPC), .Q(PC_q), .reset(Reset));  // open: Qn, preset, en
  or or_4 (or_4_out, demultiplexer_1_out0, EnIC);
  or or_5 (EnIC, START_q, PC_q);
  Demultiplexer #(.enable("false")) demultiplexer_1 (.out0(demultiplexer_1_out0), .out1(EnIF), .in(IC_q), .sel(Ready));
  D_Flip_Flop IC (.clk(Clock), .D(or_4_out), .Q(IC_q), .reset(Reset));  // open: Qn, preset, en
  or or_6 (EnRF, EN_RF0, EN_RF1);
  Demultiplexer #(.select(3), .enable("false")) demultiplexer_2 (
    .out0(demultiplexer_2_out0), .out1(BRANCH), .out2(REG_FILE), .out3(demultiplexer_2_out3),
    .out4(demultiplexer_2_out4), .out5(demultiplexer_2_out5), .in(IF_q), .sel(SELECTOR));  // open: out6, out7
  D_Flip_Flop IF (.clk(Clock), .D(EnIF), .Q(IF_q), .reset(Reset));  // open: Qn, preset, en
  and and_1 (EnTTY, ttyI, CONTINUE);
  Demultiplexer #(.enable("false")) demultiplexer_3 (
    .out0(demultiplexer_3_out0), .out1(EN_RF0), .in(demultiplexer_2_out5), .sel(R_WI));
  or or_7 (or_7_out, End, demultiplexer_2_out0);
  D_Flip_Flop u_END (.clk(Clock), .D(or_7_out), .Q(End), .reset(Reset));  // open: Qn, preset, en
  D_Flip_Flop RF (.clk(Clock), .D(EN_RF0), .Q(RF_q), .reset(Reset));  // open: Qn, preset, en
  and and_2 (EnKBD, kbdI, KBD);
  D_Flip_Flop ALU (.clk(Clock), .D(demultiplexer_2_out3), .Q(ALU_q), .reset(Reset));  // open: Qn, preset, en
  or or_8 (EnDC, demultiplexer_2_out4, demultiplexer_3_out0, RF_q);
  or or_9 (or_9_out, DC, EnDC);
  Demultiplexer #(.enable("false")) demultiplexer_4 (
    .out0(demultiplexer_4_out0), .out1(CONTINUE), .in(REG_FILE), .sel(ttyI));
  Demultiplexer #(.enable("false")) demultiplexer_5 (.out0(DC), .out1(demultiplexer_5_out1), .in(DC_q), .sel(Ready));
  D_Flip_Flop u_DC (.clk(Clock), .D(or_9_out), .Q(DC_q), .reset(Reset));  // open: Qn, preset, en
  Demultiplexer #(.enable("false")) demultiplexer_6 (
    .out0(demultiplexer_6_out0), .out1(demultiplexer_6_out1), .in(demultiplexer_5_out1), .sel(R_WI));
  or or_10 (EN_RF1, demultiplexer_4_out0, ALU_q, demultiplexer_6_out0);
  D_Flip_Flop RF_2 (.clk(Clock), .D(EN_RF1), .Q(KBD), .reset(Reset));  // open: Qn, preset, en
  or or_11 (EnPC, BRANCH, CONTINUE, KBD, demultiplexer_6_out1);

  // Other names for the same wires on the sheet: ALU_I = ALUI; CLK = Clock; EN_DC = EnDC; EN_IC = EnIC; EN_IF = EnIF;
  //   EN_KBD = EnKBD; EN_RF = EnRF; EN_TTY = EnTTY; HALT_I = halt; JMP_I = JMPI; KBD_I = kbdI; L_I = LI; EN_PC = EnPC;
  //   NEXT = EnPC; R_W_I = R_WI; S_I = SI; TR_I = TRI; TTY = CONTINUE; TTY_I = ttyI

  // Notes on the sheet:
  //   INPUTS
  //   OUTPUTS
endmodule

// CM
module CacheMemory (
  input  [31:0] RAMOut0,
  input  [31:0] RAMOut1,
  input  [31:0] Data,
  input  [17:0] Address,
  input  [31:0] RAMOut2,
  input  [31:0] RAMOut3,
  input  Clock,
  input  Reset,
  input  R_WDC,
  input  DC,
  input  EnIC,
  input  EnDC,
  input  [3:0] RT,
  input  [3:0] WT,
  output [31:0] RAMIn0,
  output [31:0] RAMIn1,
  output [31:0] M_Address,
  output [15:0] RAMAddress,
  output [31:0] RAMIn2,
  output [31:0] RAMIn3,
  output CS,
  output R_W,
  output Ready
);

  wire ASK, CS0, CS1, MATCH, or_2_out, R_W0, R_W1, READY_DC, READY_IC, TO_DC;
  wire [15:0] RAM_ADD0, RAM_ADD1;
  wire [31:0] BANK0, BANK0_O, BANK0_O0, BANK0_O1, BANK1, BANK1_O, BANK1_O0, BANK1_O1, BANK2, BANK2_O,
       BANK2_O0, BANK2_O1, BANK3, BANK3_O, BANK3_O0, BANK3_O1, DATA_BANK0, DATA_BANK1, RAM0, RAM1, RAM2, RAM3;

  or or_1 (CS, CS0, CS1);
  Multiplexer_1x32 multiplexer_1x32_1 (.Selector(CS1), .I0(BANK0_O0), .I1(BANK0_O1), .Output(BANK0_O));
  Multiplexer_1x32 multiplexer_1x32_2 (.Selector(MATCH), .I0(RAM0), .I1(BANK0_O1), .Output(BANK0));
  Little_EndianConverter little_endianconverter_1 (
    .BankIn0(RAMOut0), .BankIn1(RAMOut1), .BankIn2(RAMOut2), .BankIn3(RAMOut3), .BankOut0(RAM0),
    .BankOut1(RAM1), .BankOut2(RAM2), .BankOut3(RAM3));
  Little_EndianConverter little_endianconverter_2 (
    .BankIn0(BANK0_O), .BankIn1(BANK1_O), .BankIn2(BANK2_O), .BankIn3(BANK3_O), .BankOut0(RAMIn0),
    .BankOut1(RAMIn1), .BankOut2(RAMIn2), .BankOut3(RAMIn3));
  Multiplexer_1x16 multiplexer_1x16_1 (.Selector(CS1), .I0(RAM_ADD0), .I1(RAM_ADD1), .Output(RAMAddress));
  Multiplexer_1x32 multiplexer_1x32_3 (.Selector(CS1), .I0(BANK1_O0), .I1(BANK1_O1), .Output(BANK1_O));
  Multiplexer_1x32 multiplexer_1x32_4 (.Selector(MATCH), .I0(RAM1), .I1(BANK1_O1), .Output(BANK1));
  Multiplexer_1x32 multiplexer_1x32_5 (.Selector(READY_DC), .I0(DATA_BANK0), .I1(DATA_BANK1), .Output(M_Address));
  InstructionsCache instructionscache_1 (
    .Enable(or_2_out), .R_WDC(R_WDC), .CS(CS0), .RAMAddress(RAM_ADD0), .Bank0(BANK0), .Bank1(BANK1),
    .Data(Data), .Bank0Out(BANK0_O0), .Bank1Out(BANK1_O0), .Clock(Clock), .RT(RT), .R_W(R_W1),
    .BankData(DATA_BANK0), .Reset(Reset), .WT(WT), .Ask(ASK), .Address(Address), .Bank2(BANK2),
    .Bank3(BANK3), .Bank2Out(BANK2_O0), .Bank3Out(BANK3_O0), .Match(MATCH), .Ready(READY_IC), .EnDC(DC),
    .ToDC(TO_DC));
  or or_2 (or_2_out, EnIC, EnDC);
  Multiplexer_1x32 multiplexer_1x32_6 (.Selector(CS1), .I0(BANK2_O0), .I1(BANK2_O1), .Output(BANK2_O));
  Multiplexer_1x32 multiplexer_1x32_7 (.Selector(MATCH), .I0(RAM2), .I1(BANK2_O1), .Output(BANK2));
  or or_3 (Ready, READY_DC, READY_IC);
  Multiplexer_1x32 multiplexer_1x32_8 (.Selector(MATCH), .I0(RAM3), .I1(BANK3_O1), .Output(BANK3));
  Multiplexer_1x32 multiplexer_1x32_9 (.Selector(CS1), .I0(BANK3_O0), .I1(BANK3_O1), .Output(BANK3_O));
  or or_4 (R_W, R_W0, R_W1);
  DataCache datacache_1 (
    .R_WI(R_WDC), .Reset(Reset), .Bank0(BANK0), .Address(Address), .Bank0Out(BANK0_O1), .Bank2(BANK2),
    .Bank1(BANK1), .Bank3(BANK3), .Match(MATCH), .WT(WT), .RT(RT), .RAMAddress(RAM_ADD1), .CS(CS1),
    .R_W(R_W0), .Enable(TO_DC), .Clock(Clock), .Bank2Out(BANK2_O1), .Bank1Out(BANK1_O1), .Bank3Out(BANK3_O1),
    .Data(Data), .BankData(DATA_BANK1), .Ready(READY_DC), .Ask(ASK));

  // Other names for the same wires on the sheet: CLK = Clock; EN_DC = EnDC; EN_IC = EnIC; R_W_DC = R_WDC;
  //   RAM_ADD[15:0] = RAMAddress; RAM_IN0[31:0] = RAMIn0; RAM_IN1[31:0] = RAMIn1; RAM_IN2[31:0] = RAMIn2;
  //   RAM_IN3[31:0] = RAMIn3; RAM_OUT0[31:0] = RAMOut0; RAM_OUT1[31:0] = RAMOut1; RAM_OUT2[31:0] = RAMOut2;
  //   RAM_OUT3[31:0] = RAMOut3

  // Notes on the sheet:
  //   LITTLE-ENDIAN CONVERTER
  //   INPUTS
  //   INSTRUCTIONS CACHE
  //   OUTPUTS
  //   DATA CACHE
endmodule

// LEC
module Little_EndianConverter (
  input  [31:0] BankIn0,
  input  [31:0] BankIn1,
  input  [31:0] BankIn2,
  input  [31:0] BankIn3,
  output [31:0] BankOut0,
  output [31:0] BankOut1,
  output [31:0] BankOut2,
  output [31:0] BankOut3
);


  assign BankOut0 = {BankIn0[7:0], BankIn0[15:8], BankIn0[23:16], BankIn0[31:24]};
  assign BankOut1 = {BankIn1[7:0], BankIn1[15:8], BankIn1[23:16], BankIn1[31:24]};
  assign BankOut2 = {BankIn2[7:0], BankIn2[15:8], BankIn2[23:16], BankIn2[31:24]};
  assign BankOut3 = {BankIn3[7:0], BankIn3[15:8], BankIn3[23:16], BankIn3[31:24]};

  // Notes on the sheet:
  //   INPUTS
  //   OUTPUTS
endmodule

// DC
module DataCache (
  input  Enable,
  input  R_WI,
  input  [31:0] Bank0,
  input  [31:0] Bank1,
  input  [31:0] Data,
  input  Clock,
  input  [3:0] RT,
  input  Reset,
  input  [3:0] WT,
  input  [17:0] Address,
  input  [31:0] Bank2,
  input  [31:0] Bank3,
  input  Ask,
  output CS,
  output [15:0] RAMAddress,
  output [31:0] Bank0Out,
  output [31:0] Bank1Out,
  output R_W,
  output [31:0] BankData,
  output Match,
  output [31:0] Bank2Out,
  output [31:0] Bank3Out,
  output Ready
);

  wire _0, _1, _2, _3, and_1_out, and_2_out, and_3_out, ASKING, CONTINUE0, CONTINUE1, COUNT0, COUNT1, CS1,
       d_ff_1_q, demultiplexer_1_out0, demultiplexer_1_out1, demultiplexer_4_out0, demultiplexer_4_out1,
       demultiplexer_5_out0, demultiplexer_6_out0, demultiplexer_6_out1, DIRTY, EN_00, EN_01, EN_02, EN_03,
       EN_10, EN_11, EN_12, EN_13, EN_20, EN_21, EN_22, EN_23, EN_30, EN_31, EN_32, EN_33, EN_B0, EN_B1,
       EN_B2, EN_B3, EN_BANK0, EN_BANK1, EN_BANK2, EN_BANK3, EN_R_W, END, HIT, NEXT, or_1_out, or_4_out,
       or_8_out, or_12_out, R_W_q, RAM_R_W, VALID, WRITE, WRITE_q;
  wire [13:0] TAG_SEL, xor_1_out;
  wire [15:0] ID0_O, ID1_O, ID2_O, ID3_O;
  wire [31:0] _00_O, _01_O, _02_O, _03_O, _10_O, _11_O, _12_O, _13_O, _20_O, _21_O, _22_O, _23_O, _30_O,
       _31_O, _32_O, _33_O, DATA0, DATA1, DATA2, DATA3;

  Multiplexer_1x32 multiplexer_1x32_1 (.Selector(EN_R_W), .I0(Bank0), .I1(Data), .Output(DATA0));
  D_Flip_Flop d_ff_1 (.clk(Clock), .D(or_1_out), .Q(d_ff_1_q), .reset(Reset));  // open: Qn, preset, en
  or or_1 (or_1_out, Ask, Enable);
  or or_2 (_0, EN_BANK0, RAM_R_W);
  D_Flip_Flop u_ASK (.clk(Clock), .D(Ask), .Q(ASKING), .reset(Reset));  // open: Qn, preset, en
  Demultiplexer #(.enable("false")) demultiplexer_1 (
    .out0(demultiplexer_1_out0), .out1(demultiplexer_1_out1), .in(d_ff_1_q), .sel(and_1_out));
  Demultiplexer #(.enable("false")) demultiplexer_2 (.out0(END), .out1(WRITE), .in(demultiplexer_1_out1), .sel(R_WI));
  and and_1 (and_1_out, HIT, VALID);
  Register #(.width(16)) ID0 (.D({1'b1, EN_R_W, Address[17:4]}), .en(EN_B0), .Q(ID0_O), .clk(Clock), .clr(Reset));
  Register #(.width(16)) ID1 (.D({1'b1, EN_R_W, Address[17:4]}), .en(EN_B1), .Q(ID1_O), .clk(Clock), .clr(Reset));
  Register #(.width(16)) ID2 (.D({1'b1, EN_R_W, Address[17:4]}), .en(EN_B2), .Q(ID2_O), .clk(Clock), .clr(Reset));
  Register #(.width(16)) ID3 (.D({1'b1, EN_R_W, Address[17:4]}), .en(EN_B3), .Q(ID3_O), .clk(Clock), .clr(Reset));
  Multiplexer_1x32 multiplexer_1x32_2 (.Selector(EN_R_W), .I0(Bank1), .I1(Data), .Output(DATA1));
  Multiplexer_2x16 multiplexer_2x16_1 (
    .Selector(Address[3:2]), .I0(ID0_O), .I1(ID1_O), .I2(ID2_O), .I3(ID3_O), .Output({VALID, DIRTY, TAG_SEL}));
  and and_2 (and_2_out, DIRTY, VALID);
  Demultiplexer #(.enable("false")) demultiplexer_3 (.out0(NEXT), .out1(COUNT0), .in(and_3_out), .sel(and_2_out));
  and and_3 (and_3_out, ~ASKING, demultiplexer_1_out0);  // AND_Gate
  or or_3 (_1, EN_BANK1, RAM_R_W);
  or or_4 (or_4_out, demultiplexer_4_out0, COUNT0);
  Multiplexer_1x32 multiplexer_1x32_3 (.Selector(EN_R_W), .I0(Bank2), .I1(Data), .Output(DATA2));
  or or_5 (_2, EN_BANK2, RAM_R_W);
  D_Flip_Flop WAIT_W (.clk(Clock), .D(or_4_out), .Q(R_W), .reset(Reset));  // open: Qn, preset, en
  Register #(.width(32)) _00 (.D(DATA0), .en(EN_00), .Q(_00_O), .clk(Clock), .clr(Reset));
  Register #(.width(32)) _10 (.D(DATA0), .en(EN_10), .Q(_10_O), .clk(Clock), .clr(Reset));
  Register #(.width(32)) _20 (.D(DATA0), .en(EN_20), .Q(_20_O), .clk(Clock), .clr(Reset));
  Register #(.width(32)) _30 (.D(DATA0), .en(EN_30), .Q(_30_O), .clk(Clock), .clr(Reset));
  assign xor_1_out = Address[17:4] ^ TAG_SEL;  // XOR_Gate xor_1, 14 bits wide
  Demultiplexer #(.enable("false")) demultiplexer_4 (
    .out0(demultiplexer_4_out0), .out1(demultiplexer_4_out1), .in(R_W), .sel(CONTINUE0));
  Multiplexer_1x32 multiplexer_1x32_4 (.Selector(EN_R_W), .I0(Bank3), .I1(Data), .Output(DATA3));
  or or_6 (_3, EN_BANK3, RAM_R_W);
  Register #(.width(32)) _01 (.D(DATA1), .en(EN_01), .Q(_01_O), .clk(Clock), .clr(Reset));
  Register #(.width(32)) _11 (.D(DATA1), .en(EN_11), .Q(_11_O), .clk(Clock), .clr(Reset));
  Register #(.width(32)) _21 (.D(DATA1), .en(EN_21), .Q(_21_O), .clk(Clock), .clr(Reset));
  Register #(.width(32)) _31 (.D(DATA1), .en(EN_31), .Q(_31_O), .clk(Clock), .clr(Reset));
  nor nor_1 (HIT, xor_1_out[0], xor_1_out[1], xor_1_out[2], xor_1_out[3], xor_1_out[4], xor_1_out[5], xor_1_out[6], xor_1_out[7], xor_1_out[8], xor_1_out[9], xor_1_out[10], xor_1_out[11], xor_1_out[12], xor_1_out[13]);
  or or_7 (COUNT1, NEXT, demultiplexer_4_out1);
  or or_8 (or_8_out, demultiplexer_5_out0, COUNT1);
  Multiplexer_2x32 multiplexer_2x32_1 (
    .Selector(Address[1:0]), .I0(Bank0Out), .I1(Bank1Out), .I2(Bank2Out), .I3(Bank3Out), .Output(BankData));
  D_Flip_Flop WAIT_R (.clk(Clock), .D(or_8_out), .Q(CS1), .reset(Reset));  // open: Qn, preset, en
  Register #(.width(32)) _02 (.D(DATA2), .en(EN_02), .Q(_02_O), .clk(Clock), .clr(Reset));
  Register #(.width(32)) _12 (.D(DATA2), .en(EN_12), .Q(_12_O), .clk(Clock), .clr(Reset));
  Register #(.width(32)) _22 (.D(DATA2), .en(EN_22), .Q(_22_O), .clk(Clock), .clr(Reset));
  Register #(.width(32)) _32 (.D(DATA2), .en(EN_32), .Q(_32_O), .clk(Clock), .clr(Reset));
  Demultiplexer #(.enable("false")) demultiplexer_5 (
    .out0(demultiplexer_5_out0), .out1(RAM_R_W), .in(CS1), .sel(CONTINUE1));
  or or_9 (CS, R_W, CS1);
  Register #(.width(32)) _03 (.D(DATA3), .en(EN_03), .Q(_03_O), .clk(Clock), .clr(Reset));
  Register #(.width(32)) _13 (.D(DATA3), .en(EN_13), .Q(_13_O), .clk(Clock), .clr(Reset));
  Register #(.width(32)) _23 (.D(DATA3), .en(EN_23), .Q(_23_O), .clk(Clock), .clr(Reset));
  Register #(.width(32)) _33 (.D(DATA3), .en(EN_33), .Q(_33_O), .clk(Clock), .clr(Reset));
  and and_4 (EN_00, EN_B0, _0);
  and and_5 (EN_01, EN_B0, _1);
  and and_6 (EN_02, EN_B0, _2);
  and and_7 (EN_03, EN_B0, _3);
  D_Flip_Flop u_WRITE (.clk(Clock), .D(RAM_R_W), .Q(WRITE_q), .reset(Reset));  // open: Qn, preset, en
  Demultiplexer #(.enable("false")) demultiplexer_6 (
    .out0(demultiplexer_6_out0), .out1(demultiplexer_6_out1), .in(WRITE_q), .sel(R_WI));
  Wait wait_1 (.Clock(Clock), .Start(COUNT0), .Reset(Reset), .Time(WT), .Ready(CONTINUE0));
  or or_10 (EN_R_W, demultiplexer_6_out1, WRITE);
  and and_8 (EN_10, EN_B1, _0);
  and and_9 (EN_11, EN_B1, _1);
  and and_10 (EN_12, EN_B1, _2);
  and and_11 (EN_13, EN_B1, _3);
  D_Flip_Flop u_R_W (.clk(Clock), .D(EN_R_W), .Q(R_W_q), .reset(Reset));  // open: Qn, preset, en
  Multiplexer_2x32 multiplexer_2x32_2 (
    .Selector(Address[3:2]), .I0(_00_O), .I1(_10_O), .I2(_20_O), .I3(_30_O), .Output(Bank0Out));
  Multiplexer_2x32 multiplexer_2x32_3 (
    .Selector(Address[3:2]), .I0(_01_O), .I1(_11_O), .I2(_21_O), .I3(_31_O), .Output(Bank1Out));
  Multiplexer_2x32 multiplexer_2x32_4 (
    .Selector(Address[3:2]), .I0(_02_O), .I1(_12_O), .I2(_22_O), .I3(_32_O), .Output(Bank2Out));
  Multiplexer_2x32 multiplexer_2x32_5 (
    .Selector(Address[3:2]), .I0(_03_O), .I1(_13_O), .I2(_23_O), .I3(_33_O), .Output(Bank3Out));
  or or_11 (Ready, demultiplexer_6_out0, R_W_q, END);
  Wait wait_2 (.Clock(Clock), .Start(COUNT1), .Reset(Reset), .Time(RT), .Ready(CONTINUE1));
  and and_12 (Match, ASKING, Ready);
  and and_13 (EN_20, EN_B2, _0);
  and and_14 (EN_21, EN_B2, _1);
  and and_15 (EN_22, EN_B2, _2);
  and and_16 (EN_23, EN_B2, _3);
  Multiplexer_1x14 multiplexer_1x14_1 (.Selector(R_W), .I0(Address[17:4]), .I1(TAG_SEL), .Output(RAMAddress[15:2]));
  or or_12 (or_12_out, RAM_R_W, EN_R_W);
  Demultiplexer #(.select(2), .enable("false")) demultiplexer_7 (
    .out0(EN_B0), .out1(EN_B1), .out2(EN_B2), .out3(EN_B3), .in(or_12_out), .sel(Address[3:2]));
  Demultiplexer #(.select(2), .enable("false")) demultiplexer_8 (
    .out0(EN_BANK0), .out1(EN_BANK1), .out2(EN_BANK2), .out3(EN_BANK3), .in(EN_R_W), .sel(Address[1:0]));
  and and_17 (EN_30, EN_B3, _0);
  and and_18 (EN_31, EN_B3, _1);
  and and_19 (EN_32, EN_B3, _2);
  and and_20 (EN_33, EN_B3, _3);

  assign RAMAddress[1:0] = Address[3:2];

  // Other names for the same wires on the sheet: OFFSET[1:0] = Address[1:0]; BANK0_O[31:0] = Bank0Out;
  //   BANK1_O[31:0] = Bank1Out; BANK2_O[31:0] = Bank2Out; BANK3_O[31:0] = Bank3Out; BANK_DATA[31:0] = BankData;
  //   CLK = Clock; CS0 = R_W; EN_ID0 = EN_B0; EN_ID1 = EN_B1; EN_ID2 = EN_B2; EN_ID3 = EN_B3;
  //   ID[14:0] = {EN_R_W, Address[17:4]}; TAG[13:0] = Address[17:4]; R_W_I = R_WI; INDEX[1:0] = Address[3:2];
  //   RAM_ADD[15:0] = {RAMAddress[15:2], Address[3:2]}

  // Notes on the sheet:
  //   ID 0
  //   ID 1
  //   ID 2
  //   ID 3
  //   Index 0
  //   Index 1
  //   Index 2
  //   Index 3
  //   INPUTS
  //    0
  //    1
  //    2
  //    3
  //   OUTPUTS
endmodule

// IC
module InstructionsCache (
  input  Enable,
  input  R_WDC,
  input  [31:0] Bank0,
  input  [31:0] Bank1,
  input  [31:0] Data,
  input  Clock,
  input  [3:0] RT,
  input  Reset,
  input  [3:0] WT,
  input  [17:0] Address,
  input  [31:0] Bank2,
  input  [31:0] Bank3,
  input  Match,
  input  EnDC,
  output CS,
  output ToDC,
  output [15:0] RAMAddress,
  output [31:0] Bank0Out,
  output [31:0] Bank1Out,
  output R_W,
  output [31:0] BankData,
  output Ask,
  output [31:0] Bank2Out,
  output [31:0] Bank3Out,
  output Ready
);

  wire _0, _1, _2, _3, and_2_out, and_3_out, and_4_out, ASK0, ASK1, ASK_q, CONTINUE0, CONTINUE1, COUNT0,
       COUNT1, CS1, d_ff_1_q, DATA_R_W, demultiplexer_1_out0, demultiplexer_1_out1, demultiplexer_4_out0,
       demultiplexer_4_out1, demultiplexer_6_out0, demultiplexer_6_out1, DIRTY, EN_00, EN_01, EN_02, EN_03,
       EN_10, EN_11, EN_12, EN_13, EN_20, EN_21, EN_22, EN_23, EN_30, EN_31, EN_32, EN_33, EN_B0, EN_B1,
       EN_B2, EN_B3, EN_BANK0, EN_BANK1, EN_BANK2, EN_BANK3, END, FINISHED, FOUND, HIT, NEXT, or_3_out,
       or_7_out, or_12_out, VALID, WRITE_q;
  wire [13:0] TAG_SEL, xor_1_out;
  wire [15:0] ID0_O, ID1_O, ID2_O, ID3_O;
  wire [31:0] _00_O, _01_O, _02_O, _03_O, _10_O, _11_O, _12_O, _13_O, _20_O, _21_O, _22_O, _23_O, _30_O,
       _31_O, _32_O, _33_O, DATA0, DATA1, DATA2, DATA3;

  Multiplexer_1x32 multiplexer_1x32_1 (.Selector(ASK0), .I0(Bank0), .I1(Data), .Output(DATA0));
  and and_1 (ToDC, EnDC, demultiplexer_1_out0);
  D_Flip_Flop d_ff_1 (.clk(Clock), .D(Enable), .Q(d_ff_1_q), .reset(Reset));  // open: Qn, preset, en
  Demultiplexer #(.enable("false")) demultiplexer_1 (
    .out0(demultiplexer_1_out0), .out1(demultiplexer_1_out1), .in(d_ff_1_q), .sel(and_2_out));
  Register #(.width(16)) ID0 (.D({1'b1, ASK0, Address[17:4]}), .en(EN_B0), .Q(ID0_O), .clk(Clock), .clr(Reset));
  Register #(.width(16)) ID1 (.D({1'b1, ASK0, Address[17:4]}), .en(EN_B1), .Q(ID1_O), .clk(Clock), .clr(Reset));
  Register #(.width(16)) ID2 (.D({1'b1, ASK0, Address[17:4]}), .en(EN_B2), .Q(ID2_O), .clk(Clock), .clr(Reset));
  Register #(.width(16)) ID3 (.D({1'b1, ASK0, Address[17:4]}), .en(EN_B3), .Q(ID3_O), .clk(Clock), .clr(Reset));
  or or_1 (_0, EN_BANK0, DATA_R_W);
  Demultiplexer #(.enable("false")) demultiplexer_2 (.out0(END), .out1(ASK0), .in(demultiplexer_1_out1), .sel(R_WDC));
  and and_2 (and_2_out, HIT, VALID);
  Multiplexer_1x32 multiplexer_1x32_2 (.Selector(ASK0), .I0(Bank1), .I1(Data), .Output(DATA1));
  Multiplexer_2x16 multiplexer_2x16_1 (
    .Selector(Address[3:2]), .I0(ID0_O), .I1(ID1_O), .I2(ID2_O), .I3(ID3_O), .Output({VALID, DIRTY, TAG_SEL}));
  and and_3 (and_3_out, DIRTY, VALID);
  and and_4 (and_4_out, ~EnDC, demultiplexer_1_out0);  // AND_Gate
  Demultiplexer #(.enable("false")) demultiplexer_3 (.out0(NEXT), .out1(COUNT0), .in(and_4_out), .sel(and_3_out));
  or or_2 (_1, EN_BANK1, DATA_R_W);
  D_Flip_Flop u_R_W (.clk(Clock), .D(ASK0), .Q(FINISHED), .reset(Reset));  // open: Qn, preset, en
  or or_3 (or_3_out, demultiplexer_4_out0, COUNT0);
  Multiplexer_1x32 multiplexer_1x32_3 (.Selector(ASK0), .I0(Bank2), .I1(Data), .Output(DATA2));
  or or_4 (_2, EN_BANK2, DATA_R_W);
  assign xor_1_out = Address[17:4] ^ TAG_SEL;  // XOR_Gate xor_1, 14 bits wide
  D_Flip_Flop WAIT_W (.clk(Clock), .D(or_3_out), .Q(R_W), .reset(Reset));  // open: Qn, preset, en
  Register #(.width(32)) _00 (.D(DATA0), .en(EN_00), .Q(_00_O), .clk(Clock), .clr(Reset));
  Register #(.width(32)) _10 (.D(DATA0), .en(EN_10), .Q(_10_O), .clk(Clock), .clr(Reset));
  Register #(.width(32)) _20 (.D(DATA0), .en(EN_20), .Q(_20_O), .clk(Clock), .clr(Reset));
  Register #(.width(32)) _30 (.D(DATA0), .en(EN_30), .Q(_30_O), .clk(Clock), .clr(Reset));
  Demultiplexer #(.enable("false")) demultiplexer_4 (
    .out0(demultiplexer_4_out0), .out1(demultiplexer_4_out1), .in(R_W), .sel(CONTINUE0));
  Multiplexer_1x32 multiplexer_1x32_4 (.Selector(ASK0), .I0(Bank3), .I1(Data), .Output(DATA3));
  or or_5 (_3, EN_BANK3, DATA_R_W);
  or or_6 (ASK1, NEXT, demultiplexer_4_out1);
  Register #(.width(32)) _01 (.D(DATA1), .en(EN_01), .Q(_01_O), .clk(Clock), .clr(Reset));
  Register #(.width(32)) _11 (.D(DATA1), .en(EN_11), .Q(_11_O), .clk(Clock), .clr(Reset));
  Register #(.width(32)) _21 (.D(DATA1), .en(EN_21), .Q(_21_O), .clk(Clock), .clr(Reset));
  Register #(.width(32)) _31 (.D(DATA1), .en(EN_31), .Q(_31_O), .clk(Clock), .clr(Reset));
  nor nor_1 (HIT, xor_1_out[0], xor_1_out[1], xor_1_out[2], xor_1_out[3], xor_1_out[4], xor_1_out[5], xor_1_out[6], xor_1_out[7], xor_1_out[8], xor_1_out[9], xor_1_out[10], xor_1_out[11], xor_1_out[12], xor_1_out[13]);
  D_Flip_Flop u_ASK (.clk(Clock), .D(ASK1), .Q(ASK_q), .reset(Reset));  // open: Qn, preset, en
  Demultiplexer #(.enable("false")) demultiplexer_5 (.out0(COUNT1), .out1(FOUND), .in(ASK_q), .sel(Match));
  Multiplexer_2x32 multiplexer_2x32_1 (
    .Selector(Address[1:0]), .I0(Bank0Out), .I1(Bank1Out), .I2(Bank2Out), .I3(Bank3Out), .Output(BankData));
  or or_7 (or_7_out, demultiplexer_6_out0, COUNT1);
  Register #(.width(32)) _02 (.D(DATA2), .en(EN_02), .Q(_02_O), .clk(Clock), .clr(Reset));
  Register #(.width(32)) _12 (.D(DATA2), .en(EN_12), .Q(_12_O), .clk(Clock), .clr(Reset));
  Register #(.width(32)) _22 (.D(DATA2), .en(EN_22), .Q(_22_O), .clk(Clock), .clr(Reset));
  Register #(.width(32)) _32 (.D(DATA2), .en(EN_32), .Q(_32_O), .clk(Clock), .clr(Reset));
  or or_8 (CS, R_W, CS1);
  Demultiplexer #(.enable("false")) demultiplexer_6 (
    .out0(demultiplexer_6_out0), .out1(demultiplexer_6_out1), .in(CS1), .sel(CONTINUE1));
  D_Flip_Flop WAIT_R (.clk(Clock), .D(or_7_out), .Q(CS1), .reset(Reset));  // open: Qn, preset, en
  Register #(.width(32)) _03 (.D(DATA3), .en(EN_03), .Q(_03_O), .clk(Clock), .clr(Reset));
  Register #(.width(32)) _13 (.D(DATA3), .en(EN_13), .Q(_13_O), .clk(Clock), .clr(Reset));
  Register #(.width(32)) _23 (.D(DATA3), .en(EN_23), .Q(_23_O), .clk(Clock), .clr(Reset));
  Register #(.width(32)) _33 (.D(DATA3), .en(EN_33), .Q(_33_O), .clk(Clock), .clr(Reset));
  and and_5 (EN_00, EN_B0, _0);
  and and_6 (EN_01, EN_B0, _1);
  and and_7 (EN_02, EN_B0, _2);
  and and_8 (EN_03, EN_B0, _3);
  or or_9 (Ask, ASK0, ASK1);
  or or_10 (DATA_R_W, demultiplexer_6_out1, FOUND);
  and and_9 (EN_10, EN_B1, _0);
  and and_10 (EN_11, EN_B1, _1);
  and and_11 (EN_12, EN_B1, _2);
  and and_12 (EN_13, EN_B1, _3);
  D_Flip_Flop WRITE (.clk(Clock), .D(DATA_R_W), .Q(WRITE_q), .reset(Reset));  // open: Qn, preset, en
  Multiplexer_2x32 multiplexer_2x32_2 (
    .Selector(Address[3:2]), .I0(_00_O), .I1(_10_O), .I2(_20_O), .I3(_30_O), .Output(Bank0Out));
  Multiplexer_2x32 multiplexer_2x32_3 (
    .Selector(Address[3:2]), .I0(_01_O), .I1(_11_O), .I2(_21_O), .I3(_31_O), .Output(Bank1Out));
  Multiplexer_2x32 multiplexer_2x32_4 (
    .Selector(Address[3:2]), .I0(_02_O), .I1(_12_O), .I2(_22_O), .I3(_32_O), .Output(Bank2Out));
  Multiplexer_2x32 multiplexer_2x32_5 (
    .Selector(Address[3:2]), .I0(_03_O), .I1(_13_O), .I2(_23_O), .I3(_33_O), .Output(Bank3Out));
  Wait wait_1 (.Clock(Clock), .Start(COUNT0), .Reset(Reset), .Time(WT), .Ready(CONTINUE0));
  and and_13 (EN_20, EN_B2, _0);
  and and_14 (EN_21, EN_B2, _1);
  and and_15 (EN_22, EN_B2, _2);
  and and_16 (EN_23, EN_B2, _3);
  or or_11 (Ready, WRITE_q, END, FINISHED);
  Multiplexer_1x14 multiplexer_1x14_1 (.Selector(R_W), .I0(Address[17:4]), .I1(TAG_SEL), .Output(RAMAddress[15:2]));
  or or_12 (or_12_out, DATA_R_W, ASK0);
  Demultiplexer #(.select(2), .enable("false")) demultiplexer_7 (
    .out0(EN_B0), .out1(EN_B1), .out2(EN_B2), .out3(EN_B3), .in(or_12_out), .sel(Address[3:2]));
  Demultiplexer #(.select(2), .enable("false")) demultiplexer_8 (
    .out0(EN_BANK0), .out1(EN_BANK1), .out2(EN_BANK2), .out3(EN_BANK3), .in(ASK0), .sel(Address[1:0]));
  Wait wait_2 (.Clock(Clock), .Start(COUNT1), .Reset(Reset), .Time(RT), .Ready(CONTINUE1));
  and and_17 (EN_30, EN_B3, _0);
  and and_18 (EN_31, EN_B3, _1);
  and and_19 (EN_32, EN_B3, _2);
  and and_20 (EN_33, EN_B3, _3);

  assign RAMAddress[1:0] = Address[3:2];

  // Other names for the same wires on the sheet: OFFSET[1:0] = Address[1:0]; BANK0_O[31:0] = Bank0Out;
  //   BANK1_O[31:0] = Bank1Out; BANK2_O[31:0] = Bank2Out; BANK3_O[31:0] = Bank3Out; BANK_DATA[31:0] = BankData;
  //   CLK = Clock; CS0 = R_W; EN_DC = EnDC; EN_ID0 = EN_B0; EN_ID1 = EN_B1; EN_ID2 = EN_B2; EN_ID3 = EN_B3;
  //   ID[14:0] = {ASK0, Address[17:4]}; TAG[13:0] = Address[17:4]; EN_R_W = ASK0; R_W_DC = R_WDC;
  //   INDEX[1:0] = Address[3:2]; RAM_ADD[15:0] = {RAMAddress[15:2], Address[3:2]}; TO_DC = ToDC

  // Notes on the sheet:
  //   ID 0
  //   ID 1
  //   ID 2
  //   ID 3
  //   Index 0
  //   Index 1
  //   Index 2
  //   Index 3
  //   INPUTS
  //    0
  //    1
  //    2
  //    3
  //   OUTPUTS
endmodule

module Wait (
  input  Clock,
  input  Start,
  input  Reset,
  input  [3:0] Time,
  output Ready
);

  wire demultiplexer_1_out0, END, INC, or_1_out, or_2_out;
  wire [3:0] counter_1_q, xor_1_out;

  D_Flip_Flop COUNT (.clk(Clock), .D(demultiplexer_1_out0), .Q(INC), .preset(Start), .reset(Reset));  // open: Qn, en
  Demultiplexer #(.enable("false")) demultiplexer_1 (.out0(demultiplexer_1_out0), .out1(Ready), .in(INC), .sel(END));
  Counter #(.width(4), .max('hf)) counter_1 (
    .count(Clock), .Q(counter_1_q), .clk(Clock), .clr(or_1_out));  // open: load, D, carry
  or or_1 (or_1_out, Reset, Start);
  assign xor_1_out = Time ^ counter_1_q;  // XOR_Gate xor_1, 4 bits wide
  or or_2 (or_2_out, xor_1_out[3], xor_1_out[2], xor_1_out[1], xor_1_out[0]);
  not not_1 (END, or_2_out);

  // Other names for the same wires on the sheet: CLK = Clock

  // Notes on the sheet:
  //   INPUTS
  //   OUTPUT
endmodule

// DP
module DataPath (
  input  [6:0] kbdData,
  input  Clock,
  input  Reset,
  input  [31:0] M_Address,
  input  EnIF,
  input  EnRF,
  input  EnPC,
  input  kbdAavil,
  output [6:0] ttyData,
  output haltI,
  output JMPI,
  output TRI,
  output [17:0] Address,
  output [31:0] Data,
  output ALUI,
  output LI,
  output SI,
  output R_WI,
  output ttyI,
  output kbdI
);

  wire ADD, ADDI, ALU, alumask_1_alu, AND, and_3_out, ANDI, BEQ, BGTZ, BLEZ, BLTZ, BNE, CF, d_ff_1_q, DIV,
       DIVU, J, JR, LW, MFHI, MFLO, MULT, MULU, NOP, NOR, OF, OR, or_1_out, or_2_out, ORI, PF, POP, PUSH,
       RND, SF, SIGN, SLT, SLTI, SLTIU, SLTU, SUB, SW, TRI_t, XOR, XORI, ZF;
  wire [3:0] ALU_SEL;
  wire [4:0] multiplexer_1x5_1_output, RD, RS, RT;
  wire [15:0] OFFSET;
  wire [25:0] JMP_D;
  wire [31:0] ALU_OUT, branchcontrol_1_pc_in, HI, instructionfetcher_1_instruction, LO,
       multiplexer_1x32_1_output, PC_OUT, rfinput_1_rfin, RG_out, RT_t, SP;
  wire [31:7] RS_t;
  wire [31:31] and_2_out;

  MemoryAddress memoryaddress_1 (
    .PC_Out(PC_OUT), .ALUOut(ALU_OUT), .lw(LW), .pop(POP), .SP(SP), .Address(Address), .sw(SW), .push(PUSH));
  or or_1 (or_1_out, ADDI, LW, SW);
  BranchControl branchcontrol_1 (
    .offset(OFFSET), .PC_Out(PC_OUT), .Rs({RS_t, ttyData}), .Rt(RT_t), .jmpd(JMP_D), .beq(BEQ), .bne(BNE),
    .blez(BLEZ), .bgtz(BGTZ), .bltz(BLTZ), .jr(JR), .j(J), .PC_In(branchcontrol_1_pc_in));
  ALUMask alumask_1 (
    .add(ADD), .sub(SUB), .mult(MULT), .mulu(MULU), .div(DIV), .divu(DIVU), .\and (AND), .\or (OR),
    .\nor (NOR), .\xor (XOR), .slt(SLT), .sltu(SLTU), .addi(or_1_out), .slti(SLTI), .sltiu(SLTIU),
    .andi(ANDI), .ori(ORI), .xori(XORI), .Selector(ALU_SEL), .Sign(SIGN), .TRI(TRI_t), .ALU(alumask_1_alu));
  ProgramCounter programcounter_1 (
    .Reset(Reset), .PC_In(branchcontrol_1_pc_in), .PC_Out(PC_OUT), .Enable(EnPC), .Clock(Clock));
  and and_1 (ALU, alumask_1_alu, ~LW, ~SW);  // AND_Gate
  InstructionFetcher instructionfetcher_1 (
    .Reset(or_2_out), .Clock(Clock), .Enable(EnIF), .Instruction(instructionfetcher_1_instruction),
    .Bank(M_Address));
  or or_2 (or_2_out, d_ff_1_q, Reset);
  D_Flip_Flop d_ff_1 (.clk(Clock), .D(EnPC), .Q(d_ff_1_q));  // open: Qn, preset, en, reset
  and and_2 (and_2_out[31], ~ANDI, ~ORI, ~XORI, OFFSET[15]);  // AND_Gate
  Multiplexer_1x32 multiplexer_1x32_1 (
    .Selector(TRI_t), .I0({{16{and_2_out[31]}}, OFFSET}), .I1(RT_t), .Output(multiplexer_1x32_1_output));
  InstructionDecoder instructiondecoder_1 (
    .Instruction(instructionfetcher_1_instruction), .nop(NOP), .add(ADD), .sub(SUB), .mult(MULT),
    .mulu(MULU), .addi(ADDI), .slti(SLTI), .sltiu(SLTIU), .andi(ANDI), .j(J), .div(DIV), .divu(DIVU),
    .slt(SLT), .sltu(SLTU), .ori(ORI), .xori(XORI), .lw(LW), .sw(SW), .\and (AND), .\or (OR), .\nor (NOR),
    .\xor (XOR), .beq(BEQ), .bne(BNE), .blez(BLEZ), .bgtz(BGTZ), .bltz(BLTZ), .pop(POP), .push(PUSH),
    .jr(JR), .mfhi(MFHI), .mflo(MFLO), .halt(haltI), .tty(ttyI), .rnd(RND), .kbd(kbdI), .Rs(RS), .Rt(RT),
    .Rd(RD), .offset(OFFSET), .jmpdest(JMP_D));
  ArithmeticLogicUnit arithmeticlogicunit_1 (
    .A({RS_t, ttyData}), .B(multiplexer_1x32_1_output), .Sign(SIGN), .CF(CF), .ZF(ZF), .SF(SF),
    .Output(ALU_OUT), .Hi(HI), .Lo(LO), .Clock(Clock), .Selector(ALU_SEL), .OF(OF), .Reset(Reset), .PF(PF));
  Random #(.width(32)) RG (.clk(Clock), .next(RND), .out(RG_out));  // open: clr
  and and_3 (and_3_out, ALU, ~MULT, ~DIV);  // AND_Gate
  RFInput rfinput_1 (
    .ALUOut(ALU_OUT), .M_Address(M_Address), .Hi(HI), .Lo(LO), .RGOut(RG_out), .ALU(and_3_out), .lw(LW),
    .pop(POP), .mfhi(MFHI), .kbdData(kbdData), .mflo(MFLO), .rnd(RND), .kbd(kbdI), .kbdAvail(kbdAavil),
    .RFIn(rfinput_1_rfin));
  or or_3 (R_WI, PUSH, SW);
  or or_4 (JMPI, NOP, BEQ, BNE, BLEZ, BGTZ, BLTZ, JR, J);
  or or_5 (TRI, MFHI, MFLO, ttyI, RND, kbdI);
  RegisterFile registerfile_1 (
    .Clock(Clock), .Reset(Reset), .WIn(rfinput_1_rfin), .R_W(EnRF), .AA(RS), .AB(RT),
    .Selector(multiplexer_1x5_1_output), .A({RS_t, ttyData}), .B(RT_t), .push(PUSH), .pop(POP), .SP(SP));
  Multiplexer_1x5 multiplexer_1x5_1 (.Selector(TRI_t), .I0(RT), .I1(RD), .Output(multiplexer_1x5_1_output));
  or or_6 (ALUI, ADD, SUB, MULT, MULU, DIV, DIVU, SLT, SLTU, AND, OR, NOR, XOR, ADDI, SLTI, SLTIU, ANDI, ORI, XORI);
  or or_7 (LI, LW, SW);
  or or_8 (SI, PUSH, POP);
  Multiplexer_1x32 multiplexer_1x32_2 (.Selector(PUSH), .I0(RT_t), .I1({RS_t, ttyData}), .Output(Data));

  // Other names for the same wires on the sheet: ALU_I = ALUI; CLK = Clock; EN_IF = EnIF; EN_PC = EnPC; EN_RF = EnRF;
  //   HALT = haltI; JMP_I = JMPI; KBD = kbdI; KBD_AVAIL = kbdAavil; KBD_DATA[6:0] = kbdData; L_I = LI; R_W_I = R_WI;
  //   RS_t[6:0] = ttyData; TTY_DATA[6:0] = ttyData; S_I = SI; TR_I = TRI; TTY = ttyI

  // Notes on the sheet:
  //   INPUTS
  //   OUTPUTS
endmodule

// MA
module MemoryAddress (
  input  [31:0] PC_Out,
  input  [31:0] ALUOut,
  input  lw,
  input  push,
  input  [31:0] SP,
  input  sw,
  input  pop,
  output [17:0] Address
);

  wire [1:0] or_2_out;
  wire [31:0] multiplexer_2x32_1_output;

  Multiplexer_2x32 multiplexer_2x32_1 (
    .Selector(or_2_out), .I0(PC_Out), .I1(ALUOut), .I2(SP),
    .Output({multiplexer_2x32_1_output[31:20], Address, multiplexer_2x32_1_output[1:0]}));  // open: I3
  or or_1 (or_2_out[1], pop, push);
  or or_2 (or_2_out[0], lw, sw);

  // Other names for the same wires on the sheet: ALU_OUT[31:0] = ALUOut

  // Notes on the sheet:
  //   INPUTS
  //   OUTPUTS
endmodule

// IF
module InstructionFetcher (
  input  Reset,
  input  Clock,
  input  Enable,
  input  [31:0] Bank,
  output [31:0] Instruction
);

  Register #(.width(32)) u_BANK (.D(Bank), .en(Enable), .Q(Instruction), .clk(Clock), .clr(Reset));

  // Notes on the sheet:
  //   INPUTS
  //   OUTPUT
endmodule

// ID
module InstructionDecoder (
  input  [31:0] Instruction,
  output nop,
  output add,
  output sub,
  output mult,
  output mulu,
  output div,
  output [4:0] Rs,
  output divu,
  output slt,
  output sltu,
  output \and ,
  output \or ,
  output \nor ,
  output [4:0] Rt,
  output \xor ,
  output push,
  output pop,
  output jr,
  output mfhi,
  output mflo,
  output [4:0] Rd,
  output halt,
  output tty,
  output rnd,
  output kbd,
  output addi,
  output slti,
  output [15:0] offset,
  output sltiu,
  output andi,
  output ori,
  output xori,
  output lw,
  output sw,
  output [25:0] jmpdest,
  output beq,
  output bne,
  output blez,
  output bgtz,
  output bltz,
  output j
);

  wire _000000, _111000, _111111;

  and and_1 (_000000, ~Instruction[31], ~Instruction[30], ~Instruction[29], ~Instruction[28], ~Instruction[27], ~Instruction[26]);  // AND_Gate
  and and_2 (_111000, Instruction[29], Instruction[30], Instruction[31], ~Instruction[28], ~Instruction[27], ~Instruction[26]);  // AND_Gate
  and and_3 (_111111, Instruction[29], Instruction[30], Instruction[31], Instruction[28], Instruction[27], Instruction[26]);
  TypeRInstruction typerinstruction_1 (
    .Funct_Code(Instruction[5:0]), ._000000(_000000), .nop(nop), .add(add), .sub(sub), .mult(mult),
    .mulu(mulu), .div(div), .divu(divu), .slt(slt), .sltu(sltu), .\and (\and ), .\or (\or ), .\nor (\nor ),
    .\xor (\xor ), .pop(pop), .push(push), .jr(jr), .mfhi(mfhi), .mflo(mflo), .halt(halt), .tty(tty),
    .rnd(rnd), .kbd(kbd), ._111000(_111000), ._111111(_111111));
  TypeIInstruction typeiinstruction_1 (
    .Op_Code(Instruction[31:26]), .addi(addi), .slti(slti), .sltiu(sltiu), .andi(andi), .ori(ori),
    .xori(xori), .lw(lw), .sw(sw), .beq(beq), .bne(bne), .blez(blez), .bgtz(bgtz), .bltz(bltz));
  and and_4 (j, ~Instruction[31], ~Instruction[30], ~Instruction[29], ~Instruction[28], Instruction[27], ~Instruction[26]);  // AND_Gate

  assign jmpdest = Instruction[25:0];
  assign offset = Instruction[15:0];
  assign Rd = Instruction[15:11];
  assign Rs = Instruction[25:21];
  assign Rt = Instruction[20:16];

  // Other names for the same wires on the sheet: F_COD[5:0] = Instruction[5:0]; JMP_D[25:0] = Instruction[25:0];
  //   X[4:0] = Instruction[10:6]; _0 = Instruction[26]; OP_COD[5:0] = Instruction[31:26]; _1 = Instruction[27];
  //   _2 = Instruction[28]; _3 = Instruction[29]; _4 = Instruction[30]; _5 = Instruction[31]

  // Notes on the sheet:
  //   INPUTS
  //   OUTPUTS
endmodule

// TII
module TypeIInstruction (
  input  [5:0] Op_Code,
  output addi,
  output slti,
  output sltiu,
  output andi,
  output ori,
  output xori,
  output lw,
  output sw,
  output beq,
  output bne,
  output blez,
  output bgtz,
  output bltz
);

  and and_1 (addi, ~Op_Code[5], ~Op_Code[4], Op_Code[3], ~Op_Code[2], ~Op_Code[1], ~Op_Code[0]);  // AND_Gate
  and and_2 (ori, ~Op_Code[5], ~Op_Code[4], Op_Code[3], Op_Code[2], ~Op_Code[1], Op_Code[0]);  // AND_Gate
  and and_3 (beq, ~Op_Code[5], ~Op_Code[4], ~Op_Code[3], Op_Code[2], ~Op_Code[1], ~Op_Code[0]);  // AND_Gate
  and and_4 (slti, ~Op_Code[5], ~Op_Code[4], Op_Code[3], ~Op_Code[2], Op_Code[1], ~Op_Code[0]);  // AND_Gate
  and and_5 (xori, ~Op_Code[5], ~Op_Code[4], Op_Code[3], Op_Code[2], Op_Code[1], ~Op_Code[0]);  // AND_Gate
  and and_6 (bne, ~Op_Code[5], ~Op_Code[4], ~Op_Code[3], Op_Code[2], ~Op_Code[1], Op_Code[0]);  // AND_Gate
  and and_7 (sltiu, ~Op_Code[5], ~Op_Code[4], Op_Code[3], ~Op_Code[2], Op_Code[1], Op_Code[0]);  // AND_Gate
  and and_8 (lw, Op_Code[5], ~Op_Code[4], ~Op_Code[3], ~Op_Code[2], Op_Code[1], Op_Code[0]);  // AND_Gate
  and and_9 (blez, ~Op_Code[5], ~Op_Code[4], ~Op_Code[3], Op_Code[2], Op_Code[1], ~Op_Code[0]);  // AND_Gate
  and and_10 (andi, ~Op_Code[5], ~Op_Code[4], Op_Code[3], Op_Code[2], ~Op_Code[1], ~Op_Code[0]);  // AND_Gate
  and and_11 (sw, Op_Code[5], ~Op_Code[4], Op_Code[3], ~Op_Code[2], Op_Code[1], Op_Code[0]);  // AND_Gate
  and and_12 (bgtz, ~Op_Code[5], ~Op_Code[4], ~Op_Code[3], Op_Code[2], Op_Code[1], Op_Code[0]);  // AND_Gate
  and and_13 (bltz, ~Op_Code[5], ~Op_Code[4], ~Op_Code[3], ~Op_Code[2], ~Op_Code[1], Op_Code[0]);  // AND_Gate

  // Other names for the same wires on the sheet: _0 = Op_Code[0]; _1 = Op_Code[1]; _2 = Op_Code[2]; _3 = Op_Code[3];
  //   _4 = Op_Code[4]; _5 = Op_Code[5]

  // Notes on the sheet:
  //   INPUTS
  //   OUTPUTS
endmodule

// TRI
module TypeRInstruction (
  input  _000000,
  input  [5:0] Funct_Code,
  input  _111000,
  input  _111111,
  output nop,
  output add,
  output sub,
  output mult,
  output mulu,
  output div,
  output divu,
  output slt,
  output sltu,
  output \and ,
  output \or ,
  output \nor ,
  output \xor ,
  output pop,
  output push,
  output jr,
  output mfhi,
  output mflo,
  output halt,
  output tty,
  output rnd,
  output kbd
);

  wire and_1_out, and_17_out;

  and and_1 (and_1_out, ~Funct_Code[5], ~Funct_Code[4], ~Funct_Code[3], ~Funct_Code[2], ~Funct_Code[1], ~Funct_Code[0]);  // AND_Gate
  and and_2 (nop, _000000, and_1_out);
  and and_3 (pop, and_1_out, _111000);
  and and_4 (slt, _000000, Funct_Code[5], ~Funct_Code[4], Funct_Code[3], ~Funct_Code[2], Funct_Code[1], ~Funct_Code[0]);  // AND_Gate
  and and_5 (jr, _000000, ~Funct_Code[5], ~Funct_Code[4], Funct_Code[3], ~Funct_Code[2], ~Funct_Code[1], ~Funct_Code[0]);  // AND_Gate
  and and_6 (add, _000000, Funct_Code[5], ~Funct_Code[4], ~Funct_Code[3], ~Funct_Code[2], ~Funct_Code[1], ~Funct_Code[0]);  // AND_Gate
  and and_7 (sltu, _000000, Funct_Code[5], ~Funct_Code[4], Funct_Code[3], ~Funct_Code[2], Funct_Code[1], Funct_Code[0]);  // AND_Gate
  and and_8 (mfhi, _000000, ~Funct_Code[5], Funct_Code[4], ~Funct_Code[3], ~Funct_Code[2], ~Funct_Code[1], ~Funct_Code[0]);  // AND_Gate
  and and_9 (mflo, _000000, ~Funct_Code[5], Funct_Code[4], ~Funct_Code[3], ~Funct_Code[2], Funct_Code[1], ~Funct_Code[0]);  // AND_Gate
  and and_10 (sub, _000000, Funct_Code[5], ~Funct_Code[4], ~Funct_Code[3], ~Funct_Code[2], Funct_Code[1], ~Funct_Code[0]);  // AND_Gate
  and and_11 (\and , _000000, Funct_Code[5], ~Funct_Code[4], ~Funct_Code[3], Funct_Code[2], ~Funct_Code[1], ~Funct_Code[0]);  // AND_Gate
  and and_12 (mult, _000000, ~Funct_Code[5], Funct_Code[4], Funct_Code[3], ~Funct_Code[2], ~Funct_Code[1], ~Funct_Code[0]);  // AND_Gate
  and and_13 (\or , _000000, Funct_Code[5], ~Funct_Code[4], ~Funct_Code[3], Funct_Code[2], ~Funct_Code[1], Funct_Code[0]);  // AND_Gate
  and and_14 (halt, _111111, Funct_Code[5], Funct_Code[4], Funct_Code[3], Funct_Code[2], Funct_Code[1], Funct_Code[0]);
  and and_15 (mulu, _000000, ~Funct_Code[5], Funct_Code[4], Funct_Code[3], ~Funct_Code[2], ~Funct_Code[1], Funct_Code[0]);  // AND_Gate
  and and_16 (\nor , _000000, Funct_Code[5], ~Funct_Code[4], ~Funct_Code[3], Funct_Code[2], Funct_Code[1], Funct_Code[0]);  // AND_Gate
  and and_17 (and_17_out, ~Funct_Code[5], ~Funct_Code[4], ~Funct_Code[3], ~Funct_Code[2], ~Funct_Code[1], Funct_Code[0]);  // AND_Gate
  and and_18 (push, _111000, and_17_out);
  and and_19 (tty, and_17_out, _111111);
  and and_20 (\xor , _000000, Funct_Code[5], ~Funct_Code[4], Funct_Code[3], ~Funct_Code[2], ~Funct_Code[1], ~Funct_Code[0]);  // AND_Gate
  and and_21 (div, _000000, ~Funct_Code[5], Funct_Code[4], Funct_Code[3], ~Funct_Code[2], Funct_Code[1], ~Funct_Code[0]);  // AND_Gate
  and and_22 (rnd, _111111, ~Funct_Code[5], ~Funct_Code[4], ~Funct_Code[3], ~Funct_Code[2], Funct_Code[1], ~Funct_Code[0]);  // AND_Gate
  and and_23 (divu, _000000, ~Funct_Code[5], Funct_Code[4], Funct_Code[3], ~Funct_Code[2], Funct_Code[1], Funct_Code[0]);  // AND_Gate
  and and_24 (kbd, _111111, ~Funct_Code[5], ~Funct_Code[4], ~Funct_Code[3], Funct_Code[2], ~Funct_Code[1], ~Funct_Code[0]);  // AND_Gate

  // Other names for the same wires on the sheet: _0 = Funct_Code[0]; _1 = Funct_Code[1]; _2 = Funct_Code[2];
  //   _3 = Funct_Code[3]; _4 = Funct_Code[4]; _5 = Funct_Code[5]

  // Notes on the sheet:
  //   INPUTS
  //   OUTPUTS
endmodule

// ALUM
module ALUMask (
  input  add,
  input  sub,
  input  mult,
  input  mulu,
  input  div,
  input  divu,
  input  \and ,
  input  \or ,
  input  \nor ,
  input  \xor ,
  input  slt,
  input  sltu,
  input  addi,
  input  slti,
  input  sltiu,
  input  andi,
  input  ori,
  input  xori,
  output [3:0] Selector,
  output Sign,
  output ALU,
  output TRI
);

  wire AND_t, MULT_t, or_11_out, OR_t, SLT_t, XOR_t;

  or or_1 (Selector[3], div, divu);
  or or_2 (MULT_t, mult, mulu);
  or or_3 (SLT_t, slt, sltu, slti, sltiu);
  or or_4 (ALU, add, Selector[3], Selector[2], Selector[1], Selector[0]);
  or or_5 (AND_t, \and , andi);
  or or_6 (OR_t, \or , ori);
  or or_7 (XOR_t, \xor , xori);
  or or_8 (Selector[2], MULT_t, \nor , XOR_t, SLT_t);
  or or_9 (Selector[1], MULT_t, AND_t, OR_t, SLT_t);
  or or_10 (Selector[0], sub, MULT_t, OR_t, XOR_t);
  and and_1 (Sign, ~mulu, ~divu, ~sltu, ~sltiu);  // AND_Gate
  not not_1 (TRI, or_11_out);
  or or_11 (or_11_out, addi, slti, sltiu, andi, ori, xori);

  // Other names for the same wires on the sheet: ANDR = \and ; DIVS = div; MULTS = mult; ORR = \or ;
  //   DIV_t = Selector[3]; SLTS = slt; XORR = \xor 

  // Notes on the sheet:
  //   INPUTS
  //   OUTPUTS
endmodule

// ALU
module ArithmeticLogicUnit (
  input  Clock,
  input  Sign,
  input  [31:0] A,
  input  [31:0] B,
  input  [3:0] Selector,
  input  Reset,
  output CF,
  output OF,
  output PF,
  output [31:0] Output,
  output [31:0] Hi,
  output [31:0] Lo,
  output SF,
  output ZF
);

  wire ADD_C, ADD_R, and_6_out, and_9_out, and_10_out, and_13_out, and_14_out, and_15_out, and_16_out,
       and_17_out, and_18_out, CF1, CF2, DIV, EN, MULT, OF1, OF2, OF3, or_3_out, or_6_out, SUB_C, SUB_R,
       xor_2_out, xor_3_out, ZF0, ZF1;
  wire [0:0] SLT;
  wire [3:0] bitadder_1_out;
  wire [31:0] ADD, AND, DIV_O, DIV_R, MULT_C, MULT_O, multiplexer_1x32_1_output, multiplexer_1x32_2_output,
       NOR, OR, SUB, XOR;

  Adder #(.width(32)) adder_1 (.a(A), .b(B), .out(ADD), .cout(ADD_C));  // open: cin
  assign AND = A & B;  // AND_Gate and_1, 32 bits wide
  and and_2 (DIV, Selector[3], ~Selector[2], ~Selector[1], ~Selector[0]);  // AND_Gate
  and and_3 (CF1, ADD_C, ADD_R);
  and and_4 (CF2, SUB_C, SUB_R);
  or or_1 (EN, MULT, DIV);
  Subtractor #(.width(32)) subtractor_1 (.a(A), .b(B), .out(SUB), .bout(SUB_C));  // open: bin
  assign NOR = ~OR;  // NOT_Gate not_1, 32 bits wide
  assign OR = A | B;  // OR_Gate or_2, 32 bits wide
  Multiplexer_1x32 multiplexer_1x32_1 (.Selector(DIV), .I0(MULT_C), .I1(DIV_R), .Output(multiplexer_1x32_1_output));
  Multiplexer_1x32 multiplexer_1x32_2 (.Selector(DIV), .I0(MULT_O), .I1(DIV_O), .Output(multiplexer_1x32_2_output));
  Multiplier multiplier_1 (.A(A), .Sign(Sign), .B(B), .Output(MULT_O), .Carry(MULT_C));
  assign XOR = A ^ B;  // XOR_Gate xor_1, 32 bits wide
  Register #(.width(32)) u_HI (.D(multiplexer_1x32_1_output), .en(EN), .Q(Hi), .clk(Clock), .clr(Reset));
  Register #(.width(32)) u_LO (.D(multiplexer_1x32_2_output), .en(EN), .Q(Lo), .clk(Clock), .clr(Reset));
  or or_3 (or_3_out, MULT_C[31], MULT_C[30], MULT_C[29], MULT_C[28], MULT_C[27], MULT_C[26], MULT_C[25], MULT_C[24], MULT_C[23], MULT_C[22], MULT_C[21], MULT_C[20], MULT_C[19], MULT_C[18], MULT_C[17], MULT_C[16], MULT_C[15], MULT_C[14], MULT_C[13], MULT_C[12], MULT_C[11], MULT_C[10], MULT_C[9], MULT_C[8], MULT_C[7], MULT_C[6], MULT_C[5], MULT_C[4], MULT_C[3], MULT_C[2], MULT_C[1], MULT_C[0]);
  Divider divider_1 (.Dividend(A), .Sign(Sign), .Remainder(DIV_R), .Output(DIV_O), .Divisor(B));
  and and_5 (ADD_R, ~Selector[2], ~Selector[1], Selector[0]);  // AND_Gate
  and and_6 (and_6_out, or_3_out, MULT);
  or or_4 (CF, CF1, CF2, and_6_out);
  and and_7 (MULT, ~Selector[3], Selector[2], Selector[1], Selector[0]);  // AND_Gate
  and and_8 (SUB_R, ~Selector[2], Selector[1], ~Selector[0]);  // AND_Gate
  Comparator comparator_1 (.Sign(Sign), .A(A), .B(B), .Less(SLT[0]));
  and and_9 (and_9_out, ~A[31], ~B[31], ADD_R, SF);  // AND_Gate
  and and_10 (and_10_out, SF, SUB_R, B[31], ~A[31]);  // AND_Gate
  xor xor_2 (xor_2_out, A[31], B[31]);
  xor xor_3 (xor_3_out, xor_2_out, SF);
  or or_5 (OF1, and_9_out, and_10_out);
  and and_11 (OF3, xor_3_out, EN);
  Multiplexer_3x32 multiplexer_3x32_1 (
    .Selector(Selector[2:0]), .I0(ADD), .I1(SUB), .I2(AND), .I3(OR), .I4(NOR), .I5(XOR),
    .I6({{31{1'b0}}, SLT[0]}), .I7({32{1'b0}}), .Output(Output));
  BitAdder bitadder_1 (.in0(Output[7:0]), .out(bitadder_1_out));
  not not_2 (PF, bitadder_1_out[0]);
  and and_12 (OF, Sign, or_6_out);
  or or_6 (or_6_out, OF1, OF2, OF3);
  and and_13 (and_13_out, A[31], B[31], ADD_R, ~SF);  // AND_Gate
  and and_14 (and_14_out, ~SF, SUB_R, ~B[31], A[31]);  // AND_Gate
  or or_7 (OF2, and_13_out, and_14_out);
  nor nor_1 (ZF0, Output[31], Output[30], Output[29], Output[28], Output[27], Output[26], Output[25], Output[24], Output[23], Output[22], Output[21], Output[20], Output[19], Output[18], Output[17], Output[16], Output[15], Output[14], Output[13], Output[12], Output[11], Output[10], Output[9], Output[8], Output[7], Output[6], Output[5], Output[4], Output[3], Output[2], Output[1], Output[0]);
  and and_15 (and_15_out, Output[31], ~EN);  // AND_Gate
  and and_16 (and_16_out, Lo[31], EN);
  and and_17 (and_17_out, EN, ZF1);
  and and_18 (and_18_out, ~EN, ZF0);  // AND_Gate
  or or_8 (SF, and_15_out, and_16_out);
  or or_9 (ZF, and_17_out, and_18_out);
  nor nor_2 (ZF1, Lo[31], Lo[30], Lo[29], Lo[28], Lo[27], Lo[26], Lo[25], Lo[24], Lo[23], Lo[22], Lo[21], Lo[20], Lo[19], Lo[18], Lo[17], Lo[16], Lo[15], Lo[14], Lo[13], Lo[12], Lo[11], Lo[10], Lo[9], Lo[8], Lo[7], Lo[6], Lo[5], Lo[4], Lo[3], Lo[2], Lo[1], Lo[0]);

  // Other names for the same wires on the sheet: _0 = Selector[0]; _1 = Selector[1]; _2 = Selector[2]; A_SIGN = A[31];
  //   B_SIGN = B[31]; CLK = Clock; SF1 = Lo[31]; SF0 = Output[31]; _3 = Selector[3]

  // Notes on the sheet:
  //   INPUTS
  //   OUTPUTS
endmodule

// <
module Comparator (
  input  Sign,
  input  [31:0] A,
  input  [31:0] B,
  output Less
);

  wire and_2_out, comparator_1_lt, comparator_2_lt, LESS_U;

  Comparator_part #(.width(32), .mode("unsigned")) comparator_1 (.a(A), .b(B), .lt(comparator_1_lt));  // open: gt, eq
  and and_1 (LESS_U, comparator_1_lt, ~Sign);  // AND_Gate
  Comparator_part #(.width(32)) comparator_2 (.a(A), .b(B), .lt(comparator_2_lt));  // open: gt, eq
  or or_1 (Less, LESS_U, and_2_out);
  and and_2 (and_2_out, comparator_2_lt, Sign);

  // Notes on the sheet:
  //   INPUTS
  //   OUTPUT
endmodule

// x
module Multiplier (
  input  Sign,
  input  [31:0] A,
  input  [31:0] B,
  output [31:0] Output,
  output [31:0] Carry
);

  wire and_1_out, CARRY1, CARRY2, CARRY3;
  wire [1:0] CARRY_U;
  wire [29:0] OUTPUT_t;
  wire [31:0] adder_1_out, adder_2_out, adder_4_out, adder_5_out, CARRY_prime, CARRY_t,
       multiplexer_1x32_1_output, multiplexer_1x32_2_output, multiplexer_1x32_3_output,
       multiplexer_1x32_4_output, OUTPUT_prime;

  Multiplexer_1x32 multiplexer_1x32_1 (
    .Selector(Sign), .I0({1'b0, A[31:1]}), .I1(A), .Output(multiplexer_1x32_1_output));
  Multiplexer_1x32 multiplexer_1x32_2 (
    .Selector(Sign), .I0({1'b0, B[31:1]}), .I1(B), .Output(multiplexer_1x32_2_output));
  Multiplier_part #(.width(32)) multiplier_1 (
    .a(multiplexer_1x32_1_output), .b(multiplexer_1x32_2_output), .out({CARRY_U, OUTPUT_t}), .cout(CARRY_t));  // open: cin
  Multiplexer_1x32 multiplexer_1x32_3 (
    .Selector(A[0]), .I0({32{1'b0}}), .I1({B[31:1], 1'b0}), .Output(multiplexer_1x32_3_output));
  Adder #(.width(32)) adder_1 (
    .a({OUTPUT_t, 2'b00}), .b(multiplexer_1x32_3_output), .out(adder_1_out), .cout(CARRY1));  // open: cin
  Multiplexer_1x32 multiplexer_1x32_4 (
    .Selector(B[0]), .I0({32{1'b0}}), .I1({A[31:1], 1'b0}), .Output(multiplexer_1x32_4_output));
  Adder #(.width(32)) adder_2 (
    .a(adder_1_out), .b(multiplexer_1x32_4_output), .out(adder_2_out), .cout(CARRY2));  // open: cin
  and and_1 (and_1_out, A[0], B[0]);
  Adder #(.width(32)) adder_3 (.a(adder_2_out), .b({32{1'b0}}), .out(OUTPUT_prime), .cin(and_1_out), .cout(CARRY3));
  Adder #(.width(32)) adder_4 (
    .a({CARRY_t[29:0], CARRY_U}), .b({32{1'b0}}), .out(adder_4_out), .cin(CARRY1));  // open: cout
  Multiplexer_1x32 multiplexer_1x32_5 (.Selector(Sign), .I0(CARRY_prime), .I1(CARRY_t), .Output(Carry));
  Adder #(.width(32)) adder_5 (.a(adder_4_out), .b({32{1'b0}}), .out(adder_5_out), .cin(CARRY2));  // open: cout
  Adder #(.width(32)) adder_6 (.a({32{1'b0}}), .b(adder_5_out), .out(CARRY_prime), .cin(CARRY3));  // open: cout
  Multiplexer_1x32 multiplexer_1x32_6 (.Selector(Sign), .I0(OUTPUT_prime), .I1({CARRY_U, OUTPUT_t}), .Output(Output));

  // Other names for the same wires on the sheet: A_0 = A[0]; A_0_____0[31:1] = A[31:1]; SR_A[30:0] = A[31:1];
  //   B_0 = B[0]; B_0_____0[31:1] = B[31:1]; SR_B[30:0] = B[31:1]; CARRY_O[31:0] = Carry;
  //   CARRY_U[31:2] = CARRY_t[29:0]; OUTPUT_O[31:0] = Output; OUTPUT_t[31:30] = CARRY_U; OUTPUT_U[31:2] = OUTPUT_t

  // Notes on the sheet:
  //   INPUTS
  //   OUTPUTS
endmodule

// /
module Divider (
  input  Sign,
  input  [31:0] Dividend,
  input  [31:0] Divisor,
  output [31:0] Output,
  output [31:0] Remainder
);

  wire A_C, B_C, Q_C;
  wire [31:0] multiplexer_1x32_1_output, multiplexer_1x32_2_output, negator_1_out, negator_2_out,
       negator_3_out, negator_4_out, Q, R;

  xor xor_1 (Q_C, A_C, B_C);
  and and_1 (A_C, Dividend[31], Sign);
  and and_2 (B_C, Sign, Divisor[31]);
  Multiplexer_1x32 multiplexer_1x32_1 (
    .Selector(A_C), .I0(Dividend), .I1(negator_1_out), .Output(multiplexer_1x32_1_output));
  Negator #(.width(32)) negator_1 (.in(Dividend), .out(negator_1_out));
  Multiplexer_1x32 multiplexer_1x32_2 (
    .Selector(B_C), .I0(Divisor), .I1(negator_2_out), .Output(multiplexer_1x32_2_output));
  Negator #(.width(32)) negator_2 (.in(Divisor), .out(negator_2_out));
  Divider_part #(.width(32)) divider_1 (
    .a(multiplexer_1x32_1_output), .b(multiplexer_1x32_2_output), .out(Q), .rem(R));  // open: upper
  Negator #(.width(32)) negator_3 (.in(Q), .out(negator_3_out));
  Negator #(.width(32)) negator_4 (.in(R), .out(negator_4_out));
  Multiplexer_1x32 multiplexer_1x32_3 (.Selector(Q_C), .I0(Q), .I1(negator_3_out), .Output(Output));
  Multiplexer_1x32 multiplexer_1x32_4 (.Selector(A_C), .I0(R), .I1(negator_4_out), .Output(Remainder));

  // Other names for the same wires on the sheet: A[31:0] = Dividend; B[31:0] = Divisor; Q_prime[31:0] = Output;
  //   R_prime[31:0] = Remainder

  // Notes on the sheet:
  //   INPUTS
  //   OUTPUTS
endmodule

// RFI
module RFInput (
  input  [31:0] ALUOut,
  input  [31:0] M_Address,
  input  [31:0] Hi,
  input  [31:0] Lo,
  input  [6:0] kbdData,
  input  ALU,
  input  lw,
  input  pop,
  input  [31:0] RGOut,
  input  mfhi,
  input  mflo,
  input  rnd,
  input  kbd,
  input  kbdAvail,
  output [31:0] RFIn
);

  wire and_1_out, and_2_out, R_W;
  wire [2:0] SELECTOR;

  and and_1 (and_1_out, kbd, ~kbdAvail);  // AND_Gate
  and and_2 (and_2_out, kbd, kbdAvail);
  or or_1 (SELECTOR[2], rnd, kbd);
  or or_2 (SELECTOR[1], mfhi, mflo, and_1_out);
  or or_3 (SELECTOR[0], lw, pop, mflo, and_2_out);
  Multiplexer_3x32 multiplexer_3x32_1 (
    .Selector(SELECTOR), .I0(ALUOut), .I1(M_Address), .I2(Hi), .I3(Lo), .I4(RGOut),
    .I5({{25{1'b0}}, kbdData}), .I6({32{1'b1}}), .Output(RFIn));  // open: I7
  or or_4 (R_W, ALU, SELECTOR[2], SELECTOR[1], SELECTOR[0]);

  // Other names for the same wires on the sheet: ALU_OUT[31:0] = ALUOut; KBD_AVAIL = kbdAvail; KBD_D32[6:0] = kbdData;
  //   KBD_DATA[6:0] = kbdData; RF_IN[31:0] = RFIn; RG_OUT[31:0] = RGOut

  // Notes on the sheet:
  //   INPUTS
  //   OUTPUT
endmodule

// RF
module RegisterFile (
  input  Clock,
  input  Reset,
  input  R_W,
  input  push,
  input  pop,
  input  [31:0] WIn,
  input  [4:0] Selector,
  input  [4:0] AA,
  input  [4:0] AB,
  output [31:0] A,
  output [31:0] B,
  output [31:0] SP
);

  wire EN_R1, EN_R2, EN_R3, EN_R4, EN_R5, EN_R6, EN_R7, EN_R8, EN_R9, EN_R10, EN_R11, EN_R12, EN_R13, EN_R14,
       EN_R15, EN_R16, EN_R17, EN_R18, EN_R19, EN_R20, EN_R21, EN_R22, EN_R23, EN_R24, EN_R25, EN_R26,
       EN_R27, EN_R28, EN_R29, EN_R30, EN_R31_SP, or_1_out;
  wire [31:0] adder_1_out, R0_0__O, R1_O, R2_O, R3_O, R4_O, R5_O, R6_O, R7_O, R8_O, R9_O, R10_O, R11_O,
       R12_O, R13_O, R14_O, R15_O, R16_O, R17_O, R18_O, R19_O, R20_O, R21_O, R22_O, R23_O, R24_O, R25_O,
       R26_O, R27_O, R28_O, R29_O, R30_O, SP_IN, subtractor_1_out;

  Register #(.width(32)) R0_0 (.D(WIn), .Q(R0_0__O), .clr(Reset));  // open: en, clk
  Register #(.width(32)) R8 (.D(WIn), .en(EN_R8), .Q(R8_O), .clk(Clock), .clr(Reset));
  Register #(.width(32)) R16 (.D(WIn), .en(EN_R16), .Q(R16_O), .clk(Clock), .clr(Reset));
  Register #(.width(32)) R24 (.D(WIn), .en(EN_R24), .Q(R24_O), .clk(Clock), .clr(Reset));
  Multiplexer_5x32 multiplexer_5x32_1 (
    .Selector(AA), .I0(R0_0__O), .I1(R1_O), .I2(R2_O), .I3(R3_O), .I4(R4_O), .I5(R5_O), .I6(R6_O), .I7(R7_O),
    .I8(R8_O), .I9(R9_O), .I10(R10_O), .I11(R11_O), .I12(R12_O), .I13(R13_O), .I14(R14_O), .I15(R15_O),
    .I16(R16_O), .I17(R17_O), .I18(R18_O), .I19(R19_O), .I20(R20_O), .I21(R21_O), .I22(R22_O), .I23(R23_O),
    .I24(R24_O), .I25(R25_O), .I26(R26_O), .I27(R27_O), .I28(R28_O), .I29(R29_O), .I30(R30_O), .I31(SP),
    .Output(A));
  Register #(.width(32)) R1 (.D(WIn), .en(EN_R1), .Q(R1_O), .clk(Clock), .clr(Reset));
  Register #(.width(32)) R9 (.D(WIn), .en(EN_R9), .Q(R9_O), .clk(Clock), .clr(Reset));
  Register #(.width(32)) R17 (.D(WIn), .en(EN_R17), .Q(R17_O), .clk(Clock), .clr(Reset));
  Register #(.width(32)) R25 (.D(WIn), .en(EN_R25), .Q(R25_O), .clk(Clock), .clr(Reset));
  Multiplexer_5x32 multiplexer_5x32_2 (
    .Selector(AB), .I0(R0_0__O), .I1(R1_O), .I2(R2_O), .I3(R3_O), .I4(R4_O), .I5(R5_O), .I6(R6_O), .I7(R7_O),
    .I8(R8_O), .I9(R9_O), .I10(R10_O), .I11(R11_O), .I12(R12_O), .I13(R13_O), .I14(R14_O), .I15(R15_O),
    .I16(R16_O), .I17(R17_O), .I18(R18_O), .I19(R19_O), .I20(R20_O), .I21(R21_O), .I22(R22_O), .I23(R23_O),
    .I24(R24_O), .I25(R25_O), .I26(R26_O), .I27(R27_O), .I28(R28_O), .I29(R29_O), .I30(R30_O), .I31(SP),
    .Output(B));
  Register #(.width(32)) R2 (.D(WIn), .en(EN_R2), .Q(R2_O), .clk(Clock), .clr(Reset));
  Register #(.width(32)) R10 (.D(WIn), .en(EN_R10), .Q(R10_O), .clk(Clock), .clr(Reset));
  Register #(.width(32)) R18 (.D(WIn), .en(EN_R18), .Q(R18_O), .clk(Clock), .clr(Reset));
  Register #(.width(32)) R26 (.D(WIn), .en(EN_R26), .Q(R26_O), .clk(Clock), .clr(Reset));
  Demultiplexer #(.select(5), .enable("false")) demultiplexer_1 (
    .out1(EN_R1), .out2(EN_R2), .out3(EN_R3), .out4(EN_R4), .out5(EN_R5), .out6(EN_R6), .out7(EN_R7),
    .out8(EN_R8), .out9(EN_R9), .out10(EN_R10), .out11(EN_R11), .out12(EN_R12), .out13(EN_R13),
    .out14(EN_R14), .out15(EN_R15), .out16(EN_R16), .out17(EN_R17), .out18(EN_R18), .out19(EN_R19),
    .out20(EN_R20), .out21(EN_R21), .out22(EN_R22), .out23(EN_R23), .out24(EN_R24), .out25(EN_R25),
    .out26(EN_R26), .out27(EN_R27), .out28(EN_R28), .out29(EN_R29), .out30(EN_R30), .in(R_W), .sel(Selector));  // open: out0, out31
  Register #(.width(32)) R3 (.D(WIn), .en(EN_R3), .Q(R3_O), .clk(Clock), .clr(Reset));
  Register #(.width(32)) R11 (.D(WIn), .en(EN_R11), .Q(R11_O), .clk(Clock), .clr(Reset));
  Register #(.width(32)) R19 (.D(WIn), .en(EN_R19), .Q(R19_O), .clk(Clock), .clr(Reset));
  Register #(.width(32)) R27 (.D(WIn), .en(EN_R27), .Q(R27_O), .clk(Clock), .clr(Reset));
  Register #(.width(32)) R4 (.D(WIn), .en(EN_R4), .Q(R4_O), .clk(Clock), .clr(Reset));
  Register #(.width(32)) R12 (.D(WIn), .en(EN_R12), .Q(R12_O), .clk(Clock), .clr(Reset));
  Register #(.width(32)) R20 (.D(WIn), .en(EN_R20), .Q(R20_O), .clk(Clock), .clr(Reset));
  Register #(.width(32)) R28 (.D(WIn), .en(EN_R28), .Q(R28_O), .clk(Clock), .clr(Reset));
  and and_1 (EN_R31_SP, R_W, or_1_out);
  or or_1 (or_1_out, push, pop);
  Subtractor #(.width(32)) subtractor_1 (.a(SP), .b(32'h4), .out(subtractor_1_out));  // open: bin, bout
  Adder #(.width(32)) adder_1 (.a(32'h4), .b(SP), .out(adder_1_out));  // open: cin, cout
  Register #(.width(32)) R5 (.D(WIn), .en(EN_R5), .Q(R5_O), .clk(Clock), .clr(Reset));
  Register #(.width(32)) R13 (.D(WIn), .en(EN_R13), .Q(R13_O), .clk(Clock), .clr(Reset));
  Register #(.width(32)) R21 (.D(WIn), .en(EN_R21), .Q(R21_O), .clk(Clock), .clr(Reset));
  Register #(.width(32)) R29 (.D(WIn), .en(EN_R29), .Q(R29_O), .clk(Clock), .clr(Reset));
  Multiplexer_1x32 multiplexer_1x32_1 (.Selector(pop), .I0(subtractor_1_out), .I1(adder_1_out), .Output(SP_IN));
  Register #(.width(32)) R6 (.D(WIn), .en(EN_R6), .Q(R6_O), .clk(Clock), .clr(Reset));
  Register #(.width(32)) R14 (.D(WIn), .en(EN_R14), .Q(R14_O), .clk(Clock), .clr(Reset));
  Register #(.width(32)) R22 (.D(WIn), .en(EN_R22), .Q(R22_O), .clk(Clock), .clr(Reset));
  Register #(.width(32)) R30 (.D(WIn), .en(EN_R30), .Q(R30_O), .clk(Clock), .clr(Reset));
  Register #(.width(32)) R7 (.D(WIn), .en(EN_R7), .Q(R7_O), .clk(Clock), .clr(Reset));
  Register #(.width(32)) R15 (.D(WIn), .en(EN_R15), .Q(R15_O), .clk(Clock), .clr(Reset));
  Register #(.width(32)) R23 (.D(WIn), .en(EN_R23), .Q(R23_O), .clk(Clock));  // open: clr
  Register #(.width(32)) R31_SP (.D(SP_IN), .en(EN_R31_SP), .Q(SP), .clk(Clock), .clr(Reset));

  // Other names for the same wires on the sheet: A_A[4:0] = AA; A_B[4:0] = AB; CLK = Clock; R31_SP__O[31:0] = SP;
  //   W_IN[31:0] = WIn

  // Notes on the sheet:
  //   R0-R7
  //   R8-R15
  //   R16-R23
  //   R24-R31
  //   INPUTS
  //   Registers
  //   [SP]-4
  //   [SP]+4
  //   0 Push
  //   1 Pop
  //   OUTPUTS
endmodule

// BC
module BranchControl (
  input  [15:0] offset,
  input  [31:0] PC_Out,
  input  [31:0] Rs,
  input  [31:0] Rt,
  input  [25:0] jmpd,
  input  beq,
  input  bne,
  input  blez,
  input  bgtz,
  input  bltz,
  input  jr,
  input  j,
  output [31:0] PC_In
);

  wire and_1_out, and_2_out, and_3_out, and_4_out, and_5_out, not_1_out, not_2_out, or_2_out, RS_____0,
       RS_____0_t, RS______RT;
  wire [1:0] SELECT;
  wire [31:0] PC____4, PC____4___4_OFFSET, xor_1_out;

  nor nor_1 (RS_____0_t, Rs[31], Rs[30], Rs[29], Rs[28], Rs[27], Rs[26], Rs[25], Rs[24], Rs[23], Rs[22], Rs[21], Rs[20], Rs[19], Rs[18], Rs[17], Rs[16], Rs[15], Rs[14], Rs[13], Rs[12], Rs[11], Rs[10], Rs[9], Rs[8], Rs[7], Rs[6], Rs[5], Rs[4], Rs[3], Rs[2], Rs[1], Rs[0]);
  or or_1 (RS_____0, RS_____0_t, Rs[31]);
  assign xor_1_out = Rs ^ Rt;  // XOR_Gate xor_1, 32 bits wide
  Adder #(.width(32)) adder_1 (.a(PC_Out), .b(32'h4), .out(PC____4));  // open: cin, cout
  Adder #(.width(32)) adder_2 (
    .a(PC____4), .b({{15{offset[15]}}, offset[14:0], 2'b00}), .out(PC____4___4_OFFSET));  // open: cin, cout
  nor nor_2 (RS______RT, xor_1_out[0], xor_1_out[1], xor_1_out[2], xor_1_out[3], xor_1_out[4], xor_1_out[5], xor_1_out[6], xor_1_out[7], xor_1_out[8], xor_1_out[9], xor_1_out[10], xor_1_out[11], xor_1_out[12], xor_1_out[13], xor_1_out[14], xor_1_out[15], xor_1_out[16], xor_1_out[17], xor_1_out[18], xor_1_out[19], xor_1_out[20], xor_1_out[21], xor_1_out[22], xor_1_out[23], xor_1_out[24], xor_1_out[25], xor_1_out[26], xor_1_out[27], xor_1_out[28], xor_1_out[29], xor_1_out[30], xor_1_out[31]);
  Multiplexer_2x32 multiplexer_2x32_1 (
    .Selector(SELECT), .I0(PC____4), .I1(PC____4___4_OFFSET), .I2({PC_Out[31:28], jmpd, 2'b00}), .I3(Rs),
    .Output(PC_In));
  and and_1 (and_1_out, beq, RS______RT);
  not not_1 (not_1_out, RS______RT);
  and and_2 (and_2_out, not_1_out, bne);
  and and_3 (and_3_out, blez, RS_____0);
  not not_2 (not_2_out, RS_____0);
  and and_4 (and_4_out, not_2_out, bgtz);
  and and_5 (and_5_out, bltz, Rs[31]);
  or or_2 (or_2_out, and_1_out, and_2_out, and_3_out, and_4_out, and_5_out);
  or or_3 (SELECT[1], jr, j);
  or or_4 (SELECT[0], or_2_out, jr);

  // Other names for the same wires on the sheet: _4_OFFSET[31:2] = {{15{offset[15]}}, offset[14:0]};
  //   JMP[31:2] = {PC_Out[31:28], jmpd}; JMP_D[25:0] = jmpd; RS____0 = Rs[31]

  // Notes on the sheet:
  //   INPUTS
  //   OUTPUT
endmodule

// PC
module ProgramCounter (
  input  Reset,
  input  Clock,
  input  Enable,
  input  [31:0] PC_In,
  output [31:0] PC_Out
);

  Register #(.width(32)) PC (.D(PC_In), .en(Enable), .Q(PC_Out), .clk(Clock), .clr(Reset));

  // Notes on the sheet:
  //   INPUTS
  //   OUTPUT
endmodule

// MUX
module Multiplexer_1x5 (
  input  Selector,
  input  [4:0] I0,
  input  [4:0] I1,
  output [4:0] Output
);

  wire _0, _1;

  Decoder #(.enable("false")) decoder_1 (.out0(_0), .out1(_1), .sel(Selector));
  assign Output = _0 ? I0 : 5'bz;  // Controlled_Buffer controlled_buffer_1
  assign Output = _1 ? I1 : 5'bz;  // Controlled_Buffer controlled_buffer_2

  // Other names for the same wires on the sheet: OUT[4:0] = Output

  // Notes on the sheet:
  //   INPUTS
  //   OUTPUT
endmodule

// MUX
module Multiplexer_1x14 (
  input  Selector,
  input  [13:0] I0,
  input  [13:0] I1,
  output [13:0] Output
);

  wire _0, _1;

  Decoder #(.enable("false")) decoder_1 (.out0(_0), .out1(_1), .sel(Selector));
  assign Output = _0 ? I0 : 14'bz;  // Controlled_Buffer controlled_buffer_1
  assign Output = _1 ? I1 : 14'bz;  // Controlled_Buffer controlled_buffer_2

  // Other names for the same wires on the sheet: OUT[13:0] = Output

  // Notes on the sheet:
  //   INPUTS
  //   OUTPUT
endmodule

// MUX
module Multiplexer_1x16 (
  input  Selector,
  input  [15:0] I0,
  input  [15:0] I1,
  output [15:0] Output
);

  wire _0, _1;

  Decoder #(.enable("false")) decoder_1 (.out0(_0), .out1(_1), .sel(Selector));
  assign Output = _0 ? I0 : 16'bz;  // Controlled_Buffer controlled_buffer_1
  assign Output = _1 ? I1 : 16'bz;  // Controlled_Buffer controlled_buffer_2

  // Other names for the same wires on the sheet: OUT[15:0] = Output

  // Notes on the sheet:
  //   INPUTS
  //   OUTPUT
endmodule

// MUX
module Multiplexer_1x32 (
  input  Selector,
  input  [31:0] I0,
  input  [31:0] I1,
  output [31:0] Output
);

  wire _0, _1;

  Decoder #(.enable("false")) decoder_1 (.out0(_0), .out1(_1), .sel(Selector));
  assign Output = _0 ? I0 : 32'bz;  // Controlled_Buffer controlled_buffer_1
  assign Output = _1 ? I1 : 32'bz;  // Controlled_Buffer controlled_buffer_2

  // Other names for the same wires on the sheet: OUT[31:0] = Output

  // Notes on the sheet:
  //   INPUTS
  //   OUTPUT
endmodule

// MUX
module Multiplexer_2x16 (
  input  [1:0] Selector,
  input  [15:0] I0,
  input  [15:0] I1,
  input  [15:0] I2,
  input  [15:0] I3,
  output [15:0] Output
);

  wire _0, _1, _2, _3;

  Decoder #(.select(2), .enable("false")) decoder_1 (.out0(_0), .out1(_1), .out2(_2), .out3(_3), .sel(Selector));
  assign Output = _0 ? I0 : 16'bz;  // Controlled_Buffer controlled_buffer_1
  assign Output = _1 ? I1 : 16'bz;  // Controlled_Buffer controlled_buffer_2
  assign Output = _2 ? I2 : 16'bz;  // Controlled_Buffer controlled_buffer_3
  assign Output = _3 ? I3 : 16'bz;  // Controlled_Buffer controlled_buffer_4

  // Other names for the same wires on the sheet: OUT[15:0] = Output

  // Notes on the sheet:
  //   INPUTS
  //   OUTPUT
endmodule

// MUX
module Multiplexer_2x32 (
  input  [1:0] Selector,
  input  [31:0] I0,
  input  [31:0] I1,
  input  [31:0] I2,
  input  [31:0] I3,
  output [31:0] Output
);

  wire _0, _1, _2, _3;

  Decoder #(.select(2), .enable("false")) decoder_1 (.out0(_0), .out1(_1), .out2(_2), .out3(_3), .sel(Selector));
  assign Output = _0 ? I0 : 32'bz;  // Controlled_Buffer controlled_buffer_1
  assign Output = _1 ? I1 : 32'bz;  // Controlled_Buffer controlled_buffer_2
  assign Output = _2 ? I2 : 32'bz;  // Controlled_Buffer controlled_buffer_3
  assign Output = _3 ? I3 : 32'bz;  // Controlled_Buffer controlled_buffer_4

  // Other names for the same wires on the sheet: OUT[31:0] = Output

  // Notes on the sheet:
  //   INPUTS
  //   OUTPUT
endmodule

// MUX
module Multiplexer_3x32 (
  input  [2:0] Selector,
  input  [31:0] I0,
  input  [31:0] I1,
  input  [31:0] I2,
  input  [31:0] I3,
  input  [31:0] I4,
  input  [31:0] I5,
  input  [31:0] I6,
  input  [31:0] I7,
  output [31:0] Output
);

  wire _0, _1, _2, _3, _4, _5, _6, _7;

  assign Output = _0 ? I0 : 32'bz;  // Controlled_Buffer controlled_buffer_1
  assign Output = _4 ? I4 : 32'bz;  // Controlled_Buffer controlled_buffer_2
  Decoder #(.select(3), .enable("false")) decoder_1 (
    .out0(_0), .out1(_1), .out2(_2), .out3(_3), .out4(_4), .out5(_5), .out6(_6), .out7(_7), .sel(Selector));
  assign Output = _1 ? I1 : 32'bz;  // Controlled_Buffer controlled_buffer_3
  assign Output = _5 ? I5 : 32'bz;  // Controlled_Buffer controlled_buffer_4
  assign Output = _2 ? I2 : 32'bz;  // Controlled_Buffer controlled_buffer_5
  assign Output = _6 ? I6 : 32'bz;  // Controlled_Buffer controlled_buffer_6
  assign Output = _3 ? I3 : 32'bz;  // Controlled_Buffer controlled_buffer_7
  assign Output = _7 ? I7 : 32'bz;  // Controlled_Buffer controlled_buffer_8

  // Other names for the same wires on the sheet: OUT[31:0] = Output

  // Notes on the sheet:
  //   INPUTS
  //   OUTPUT
endmodule

// MUX
module Multiplexer_5x32 (
  input  [4:0] Selector,
  input  [31:0] I0,
  input  [31:0] I1,
  input  [31:0] I2,
  input  [31:0] I3,
  input  [31:0] I4,
  input  [31:0] I5,
  input  [31:0] I6,
  input  [31:0] I7,
  input  [31:0] I8,
  input  [31:0] I9,
  input  [31:0] I10,
  input  [31:0] I11,
  input  [31:0] I12,
  input  [31:0] I13,
  input  [31:0] I14,
  input  [31:0] I15,
  input  [31:0] I16,
  input  [31:0] I17,
  input  [31:0] I18,
  input  [31:0] I19,
  input  [31:0] I20,
  input  [31:0] I21,
  input  [31:0] I22,
  input  [31:0] I23,
  input  [31:0] I24,
  input  [31:0] I25,
  input  [31:0] I26,
  input  [31:0] I27,
  input  [31:0] I28,
  input  [31:0] I29,
  input  [31:0] I30,
  input  [31:0] I31,
  output [31:0] Output
);

  wire _0, _1, _2, _3, _4, _5, _6, _7, _8, _9, _10, _11, _12, _13, _14, _15, _16, _17, _18, _19, _20, _21,
       _22, _23, _24, _25, _26, _27, _28, _29, _30, _31;

  assign Output = _0 ? I0 : 32'bz;  // Controlled_Buffer controlled_buffer_1
  assign Output = _4 ? I4 : 32'bz;  // Controlled_Buffer controlled_buffer_2
  assign Output = _8 ? I8 : 32'bz;  // Controlled_Buffer controlled_buffer_3
  assign Output = _12 ? I12 : 32'bz;  // Controlled_Buffer controlled_buffer_4
  assign Output = _16 ? I16 : 32'bz;  // Controlled_Buffer controlled_buffer_5
  assign Output = _20 ? I20 : 32'bz;  // Controlled_Buffer controlled_buffer_6
  assign Output = _24 ? I24 : 32'bz;  // Controlled_Buffer controlled_buffer_7
  assign Output = _28 ? I28 : 32'bz;  // Controlled_Buffer controlled_buffer_8
  assign Output = _1 ? I1 : 32'bz;  // Controlled_Buffer controlled_buffer_9
  assign Output = _5 ? I5 : 32'bz;  // Controlled_Buffer controlled_buffer_10
  assign Output = _9 ? I9 : 32'bz;  // Controlled_Buffer controlled_buffer_11
  assign Output = _13 ? I13 : 32'bz;  // Controlled_Buffer controlled_buffer_12
  assign Output = _17 ? I17 : 32'bz;  // Controlled_Buffer controlled_buffer_13
  assign Output = _21 ? I21 : 32'bz;  // Controlled_Buffer controlled_buffer_14
  assign Output = _25 ? I25 : 32'bz;  // Controlled_Buffer controlled_buffer_15
  assign Output = _29 ? I29 : 32'bz;  // Controlled_Buffer controlled_buffer_16
  Decoder #(.select(5), .enable("false")) decoder_1 (
    .out0(_0), .out1(_1), .out2(_2), .out3(_3), .out4(_4), .out5(_5), .out6(_6), .out7(_7), .out8(_8),
    .out9(_9), .out10(_10), .out11(_11), .out12(_12), .out13(_13), .out14(_14), .out15(_15), .out16(_16),
    .out17(_17), .out18(_18), .out19(_19), .out20(_20), .out21(_21), .out22(_22), .out23(_23), .out24(_24),
    .out25(_25), .out26(_26), .out27(_27), .out28(_28), .out29(_29), .out30(_30), .out31(_31), .sel(Selector));
  assign Output = _2 ? I2 : 32'bz;  // Controlled_Buffer controlled_buffer_17
  assign Output = _6 ? I6 : 32'bz;  // Controlled_Buffer controlled_buffer_18
  assign Output = _10 ? I10 : 32'bz;  // Controlled_Buffer controlled_buffer_19
  assign Output = _14 ? I14 : 32'bz;  // Controlled_Buffer controlled_buffer_20
  assign Output = _18 ? I18 : 32'bz;  // Controlled_Buffer controlled_buffer_21
  assign Output = _22 ? I22 : 32'bz;  // Controlled_Buffer controlled_buffer_22
  assign Output = _26 ? I26 : 32'bz;  // Controlled_Buffer controlled_buffer_23
  assign Output = _30 ? I30 : 32'bz;  // Controlled_Buffer controlled_buffer_24
  assign Output = _3 ? I3 : 32'bz;  // Controlled_Buffer controlled_buffer_25
  assign Output = _7 ? I7 : 32'bz;  // Controlled_Buffer controlled_buffer_26
  assign Output = _11 ? I11 : 32'bz;  // Controlled_Buffer controlled_buffer_27
  assign Output = _15 ? I15 : 32'bz;  // Controlled_Buffer controlled_buffer_28
  assign Output = _19 ? I19 : 32'bz;  // Controlled_Buffer controlled_buffer_29
  assign Output = _23 ? I23 : 32'bz;  // Controlled_Buffer controlled_buffer_30
  assign Output = _27 ? I27 : 32'bz;  // Controlled_Buffer controlled_buffer_31
  assign Output = _31 ? I31 : 32'bz;  // Controlled_Buffer controlled_buffer_32

  // Other names for the same wires on the sheet: OUT[31:0] = Output

  // Notes on the sheet:
  //   INPUTS
  //   OUTPUT
endmodule
